// Logisim project 3.circ as structural Verilog
module \_3输入多数表决器  (
  input  X,
  input  Y,
  input  Z,
  output out_4
);

  wire and_1_out, and_2_out, and_3_out;

  and and_1 (and_1_out, Y, Z);
  and and_2 (and_2_out, X, Z);
  and and_3 (and_3_out, X, Y);
  or or_1 (out_4, and_1_out, and_2_out, and_3_out);
endmodule

module \晶体管构建两输入或门  (
  input  X,
  input  Y,
  output out_3
);

  wire transistor_1_out, transistor_2_out;

  Transistor transistor_1 (.in(1'b1), .out(transistor_1_out), .gate(X));
  Transistor transistor_2 (.in(transistor_1_out), .out(transistor_2_out), .gate(Y));
  Transistor #(.\type ("n")) transistor_3 (.in(1'b0), .out(transistor_2_out), .gate(X));
  Transistor #(.\type ("n")) transistor_4 (.in(1'b0), .out(transistor_2_out), .gate(Y));
  Transistor transistor_5 (.in(1'b1), .out(out_3), .gate(transistor_2_out));
  Transistor #(.\type ("n")) transistor_6 (.in(1'b0), .out(out_3), .gate(transistor_2_out));
endmodule
