// Logisim project 判断奇偶.circ as structural Verilog: 2 circuits, main circuit main
module main (
  input  in_1,
  input  in_2,
  input  in_3,
  input  in_4,
  output \偶数 ,
  output \奇数 
);

  wire xor_1_out, xor_2_out;

  xor xor_1 (xor_1_out, in_1, in_2);
  xor xor_2 (xor_2_out, in_3, in_4);
  xor xor_3 (\偶数 , xor_1_out, xor_2_out);
  not not_1 (\奇数 , \偶数 );
endmodule

module demo (
  input  a,
  input  b,
  input  c,
  input  d,
  output \偶数 ,
  output \奇数 
);

  wire and_1_out, and_2_out, and_3_out, and_4_out, and_5_out, and_6_out, and_7_out, and_8_out, and_9_out,
       and_10_out, and_11_out, and_12_out, and_13_out, and_14_out, and_15_out, and_16_out, not_1_out,
       not_2_out, not_3_out, not_4_out, not_5_out, not_6_out, not_7_out, not_8_out, not_9_out, not_10_out,
       not_11_out, not_12_out, not_13_out, not_14_out, not_15_out, not_16_out, not_17_out, not_18_out,
       not_19_out, not_20_out, not_21_out, not_22_out, not_23_out, not_24_out, not_25_out, not_26_out,
       not_27_out, not_28_out, not_29_out, not_30_out, not_31_out, not_32_out;

  not not_1 (not_1_out, a);
  not not_2 (not_2_out, b);
  not not_3 (not_3_out, c);
  not not_4 (not_4_out, a);
  not not_5 (not_5_out, b);
  not not_6 (not_6_out, d);
  not not_7 (not_7_out, a);
  not not_8 (not_8_out, c);
  not not_9 (not_9_out, d);
  not not_10 (not_10_out, a);
  not not_11 (not_11_out, b);
  not not_12 (not_12_out, c);
  not not_13 (not_13_out, d);
  not not_14 (not_14_out, b);
  not not_15 (not_15_out, c);
  not not_16 (not_16_out, d);
  not not_17 (not_17_out, a);
  not not_18 (not_18_out, b);
  not not_19 (not_19_out, c);
  not not_20 (not_20_out, d);
  not not_21 (not_21_out, a);
  not not_22 (not_22_out, b);
  not not_23 (not_23_out, a);
  not not_24 (not_24_out, c);
  not not_25 (not_25_out, a);
  not not_26 (not_26_out, d);
  not not_27 (not_27_out, b);
  not not_28 (not_28_out, c);
  not not_29 (not_29_out, b);
  not not_30 (not_30_out, d);
  not not_31 (not_31_out, c);
  not not_32 (not_32_out, d);
  and and_1 (and_1_out, not_1_out, not_2_out, not_3_out, d);
  and and_2 (and_2_out, not_4_out, not_5_out, c, not_6_out);
  and and_3 (and_3_out, not_7_out, b, not_8_out, not_9_out);
  and and_4 (and_4_out, not_10_out, b, c, d);
  and and_5 (and_5_out, a, not_11_out, not_12_out, not_13_out);
  and and_6 (and_6_out, a, not_14_out, c, d);
  and and_7 (and_7_out, a, b, not_15_out, d);
  and and_8 (and_8_out, a, b, c, not_16_out);
  and and_9 (and_9_out, not_17_out, not_18_out, not_19_out, not_20_out);
  and and_10 (and_10_out, not_21_out, not_22_out, c, d);
  and and_11 (and_11_out, not_23_out, b, not_24_out, d);
  and and_12 (and_12_out, not_25_out, b, c, not_26_out);
  and and_13 (and_13_out, a, not_27_out, not_28_out, d);
  and and_14 (and_14_out, a, not_29_out, c, not_30_out);
  and and_15 (and_15_out, a, b, not_31_out, not_32_out);
  and and_16 (and_16_out, a, b, c, d);
  or or_1 (\偶数 , and_1_out, and_2_out, and_3_out, and_4_out, and_5_out, and_6_out, and_7_out, and_8_out);
  or or_2 (\奇数 , and_9_out, and_10_out, and_11_out, and_12_out, and_13_out, and_14_out, and_15_out, and_16_out);
endmodule
