// Logisim project 8-3优先级编码器.circ as structural Verilog: 1 circuit, main circuit main
module main (
  input  I0,
  input  I1,
  input  I2,
  input  I3,
  input  I4,
  input  I5,
  input  I6,
  input  I7
);

  wire _0_out, _1_out, _2_out, _3_out, _4_out, _5_out, _6_out;
  wire [2:0] o2_out;

  and _0 (_0_out, ~I0, I1);  // AND_Gate
  and _1 (_1_out, ~I0, ~I1, I2);  // AND_Gate
  or o0 (o2_out[2], _4_out, _5_out, _3_out, _6_out);
  and _2 (_2_out, ~I0, ~I1, ~I2, I3);  // AND_Gate
  and _3 (_3_out, ~I0, ~I1, ~I2, ~I3, I4);  // AND_Gate
  or o1 (o2_out[1], _5_out, _1_out, _2_out, _6_out);
  and _4 (_4_out, ~I0, ~I1, ~I2, ~I3, ~I4, I5);  // AND_Gate
  and _5 (_5_out, ~I0, ~I1, ~I2, ~I3, ~I4, ~I5, I6);  // AND_Gate
  or o2 (o2_out[0], _0_out, _2_out, _4_out, _6_out);
  and _6 (_6_out, ~I0, ~I1, ~I2, ~I3, ~I4, ~I5, ~I6, I7);  // AND_Gate
  Hex_Digit_Display hex_digit_display_1 (.value({1'b0, o2_out}));  // open: dp
endmodule
