// Logisim project ALU.circ as structural Verilog: 4 circuits, main circuit main
module main (
  input  A,
  input  B,
  input  s3,
  input  s2,
  input  s1,
  output cout,
  output out_7
);

  wire and_1_out, minor_1_cout, minor_1_s, not_1_out, not_2_out, not_3_out, or_1_out, plus_1_s, xor_1_out;

  not not_1 (not_1_out, B);
  not not_2 (not_2_out, A);
  not not_3 (not_3_out, B);
  or or_1 (or_1_out, A, B);
  xor xor_1 (xor_1_out, A, not_1_out);
  plus plus_1 (.A(B), .B(A), .S(plus_1_s), .Cout(cout));
  minor minor_1 (.A(A), .B(B), .S(minor_1_s), .Cout(minor_1_cout));
  and and_1 (and_1_out, A, B);
  _8_1 u_8_1_1 (
    ._0(plus_1_s), ._1(minor_1_s), ._2(and_1_out), ._3(or_1_out), ._4(xor_1_out), ._5(not_2_out), ._6(A),
    ._7(not_3_out), .s0(s1), .s1(s2), .s2(s3), .out_12(out_7));
endmodule

module _8_1 (
  input  _0,
  input  _1,
  input  _2,
  input  _3,
  input  _4,
  input  _5,
  input  _6,
  input  _7,
  input  s0,
  input  s1,
  input  s2,
  output out_12
);

  wire nand_1_out, nand_2_out, nand_3_out, nand_4_out, nand_5_out, nand_6_out, nand_7_out, nand_8_out,
       nand_9_out, nand_10_out, nor_1_out, not_1_out, not_2_out, not_3_out;

  not not_1 (not_1_out, s0);
  not not_2 (not_2_out, s1);
  not not_3 (not_3_out, s2);
  nand nand_1 (nand_1_out, not_3_out, not_2_out, not_1_out, _0);
  nand nand_2 (nand_2_out, s2, not_2_out, not_1_out, _4);
  nand nand_3 (nand_3_out, not_3_out, s1, not_1_out, _2);
  nand nand_4 (nand_4_out, s2, s1, not_1_out, _6);
  nand nand_5 (nand_5_out, not_3_out, not_2_out, s0, _1);
  nand nand_6 (nand_6_out, s2, not_2_out, s0, _5);
  nand nand_7 (nand_7_out, not_3_out, s1, s0, _3);
  nand nand_8 (nand_8_out, s2, s1, s0, _7);
  nand nand_9 (nand_9_out, nand_1_out, nand_2_out, nand_3_out, nand_4_out);
  nand nand_10 (nand_10_out, nand_5_out, nand_6_out, nand_7_out, nand_8_out);
  nor nor_1 (nor_1_out, nand_9_out, nand_10_out);
  not not_4 (out_12, nor_1_out);
endmodule

module plus (
  input  A,
  input  B,
  output S,
  output Cout
);

  wire and_2_out, and_3_out, not_1_out, not_2_out;

  not not_1 (not_1_out, A);
  not not_2 (not_2_out, B);
  and and_1 (Cout, A, B);
  and and_2 (and_2_out, not_1_out, B);
  and and_3 (and_3_out, A, not_2_out);
  or or_1 (S, and_2_out, and_3_out);
endmodule

module minor (
  input  A,
  input  B,
  output S,
  output Cout
);

  wire and_1_out, and_2_out, not_1_out, not_2_out, not_3_out;

  not not_1 (not_1_out, A);
  not not_2 (not_2_out, B);
  not not_3 (not_3_out, A);
  and and_1 (and_1_out, not_1_out, B);
  and and_2 (and_2_out, A, not_2_out);
  and and_3 (Cout, not_3_out, B);
  or or_1 (S, and_1_out, and_2_out);
endmodule
