// Logisim project NJUCS.circ as structural Verilog: 1 circuit, main circuit main
module main (
  input  [6:0] in_1,
  input  [6:0] in_2,
  input  [6:0] in_3,
  input  [6:0] in_4,
  input  [6:0] in_5,
  input  [6:0] in_6,
  input  [6:0] in_7,
  input  [6:0] in_8,
  input  [6:0] in_9,
  input  [6:0] in_10,
  input  [6:0] in_11,
  input  [6:0] in_12,
  input  [6:0] in_13,
  input  [6:0] in_14,
  input  [6:0] in_15,
  input  [6:0] in_16,
  input  [6:0] in_17,
  input  [6:0] in_18,
  input  [6:0] in_19,
  input  [6:0] in_20,
  input  [6:0] in_21,
  input  [6:0] in_22,
  input  [6:0] in_23,
  input  [6:0] in_24,
  input  [6:0] in_25,
  input  [6:0] in_26,
  input  [6:0] in_27,
  input  [6:0] in_28,
  input  [6:0] in_29,
  input  [6:0] in_30
);

  LED led_1 ();  // open: in
  DotMatrix dotmatrix_1 (.col0(in_1), .col1(in_3), .col2(in_5), .col3(in_7), .col4(in_9));
  DotMatrix dotmatrix_2 (.col0(in_11), .col1(in_13), .col2(in_15), .col3(in_17), .col4(in_19));
  DotMatrix dotmatrix_3 (.col0(in_21), .col1(in_22), .col2(in_23), .col3(in_24), .col4(in_25));
  DotMatrix dotmatrix_4 (.col0(in_20), .col1(in_18), .col2(in_16), .col3(in_14), .col4(in_12));
  DotMatrix dotmatrix_5 (.col0(in_26), .col1(in_27), .col2(in_28), .col3(in_29), .col4(in_30));
  DotMatrix dotmatrix_6 (.col0(in_10), .col1(in_8), .col2(in_6), .col3(in_4), .col4(in_2));
endmodule
