// Logisim project 全加器.circ as structural Verilog: 2 circuits, main circuit main
// 全加器
module main (
  input  A,
  input  B,
  input  Cin,
  output S,
  output Cout
);

  wire and_1_out, and_2_out, xor_1_out;

  xor xor_1 (xor_1_out, A, B);
  and and_1 (and_1_out, B, A);
  and and_2 (and_2_out, Cin, xor_1_out);
  xor xor_2 (S, xor_1_out, Cin);
  or or_1 (Cout, and_2_out, and_1_out);
endmodule

module \_4位  (
  input  A1,
  input  B1,
  input  Cin,
  input  A2,
  input  B2,
  input  A3,
  input  B3,
  input  A4,
  input  B4,
  output Sum1,
  output Sum2,
  output Sum3,
  output Sum4,
  output Cout
);

  wire main_1_cout, main_2_cout, main_3_cout;

  Hex_Digit_Display hex_digit_display_1 (.value({A4, A3, A2, A1}));  // open: dp
  Hex_Digit_Display hex_digit_display_2 (.value({B4, B3, B2, B1}));  // open: dp
  main main_1 (.A(A1), .B(B1), .Cin(Cin), .S(Sum1), .Cout(main_1_cout));
  main main_2 (.A(A2), .B(B2), .Cin(main_1_cout), .S(Sum2), .Cout(main_2_cout));
  main main_3 (.A(A3), .B(B3), .Cin(main_2_cout), .S(Sum3), .Cout(main_3_cout));
  main main_4 (.A(A4), .B(B4), .Cin(main_3_cout), .S(Sum4), .Cout(Cout));
  Hex_Digit_Display hex_digit_display_3 (.value({3'b000, Cout}));  // open: dp
  Hex_Digit_Display hex_digit_display_4 (.value({Sum4, Sum3, Sum2, Sum1}));  // open: dp
endmodule
