// Logisim project 2.circ as structural Verilog: 3 circuits, main circuit main
module main (
  input  CLK,
  input  CLR,
  input  LIN,
  input  D,
  input  C,
  input  B,
  input  S1,
  input  S0,
  input  A,
  input  RIN,
  output QD,
  output QC,
  output QB,
  output QA
);

  wire and_1_out, and_2_out, and_3_out, and_4_out, and_5_out, and_6_out, and_7_out, and_8_out, and_9_out,
       and_10_out, and_11_out, and_12_out, and_13_out, and_14_out, and_15_out, and_16_out, not_1_out,
       not_2_out, not_3_out, not_4_out, not_5_out, not_6_out, or_1_out, or_2_out, or_3_out, or_4_out;

  not not_1 (not_1_out, CLK);
  not not_2 (not_2_out, CLR);
  not not_3 (not_3_out, S1);
  not not_4 (not_4_out, S0);
  not not_5 (not_5_out, not_3_out);
  not not_6 (not_6_out, not_4_out);
  and and_1 (and_1_out, not_2_out, LIN, not_5_out, not_4_out);
  and and_2 (and_2_out, not_2_out, QD, not_3_out, not_4_out);
  and and_3 (and_3_out, not_2_out, D, not_5_out, not_6_out);
  and and_4 (and_4_out, not_2_out, QC, not_3_out, not_6_out);
  and and_5 (and_5_out, not_2_out, QD, not_5_out, not_4_out);
  and and_6 (and_6_out, not_2_out, QC, not_3_out, not_4_out);
  and and_7 (and_7_out, not_2_out, C, not_5_out, not_6_out);
  and and_8 (and_8_out, not_2_out, QB, not_3_out, not_6_out);
  and and_9 (and_9_out, not_2_out, QC, not_5_out, not_4_out);
  and and_10 (and_10_out, not_2_out, QB, not_3_out, not_4_out);
  and and_11 (and_11_out, not_2_out, B, not_5_out, not_6_out);
  and and_12 (and_12_out, not_2_out, QA, not_3_out, not_6_out);
  and and_13 (and_13_out, not_2_out, QB, not_5_out, not_4_out);
  and and_14 (and_14_out, not_2_out, QA, not_3_out, not_4_out);
  and and_15 (and_15_out, not_2_out, A, not_5_out, not_6_out);
  and and_16 (and_16_out, not_2_out, RIN, not_3_out, not_6_out);
  or or_1 (or_1_out, and_1_out, and_2_out, and_3_out, and_4_out);
  or or_2 (or_2_out, and_5_out, and_6_out, and_7_out, and_8_out);
  or or_3 (or_3_out, and_9_out, and_10_out, and_11_out, and_12_out);
  or or_4 (or_4_out, and_13_out, and_14_out, and_15_out, and_16_out);
  D_Flip_Flop d_ff_1 (.clk(not_1_out), .D(or_1_out), .Q(QD));  // open: Qn, preset, reset
  D_Flip_Flop d_ff_2 (.clk(not_1_out), .D(or_2_out), .Q(QC));  // open: Qn, preset, reset
  D_Flip_Flop d_ff_3 (.clk(not_1_out), .D(or_3_out), .Q(QB));  // open: Qn, preset, reset
  D_Flip_Flop d_ff_4 (.clk(not_1_out), .D(or_4_out), .Q(QA));  // open: Qn, preset, reset
endmodule

module fankui (
  input  QD,
  input  QC,
  input  QB,
  input  QA,
  output x
);

  wire and_1_out, and_2_out, and_3_out, not_1_out, not_2_out, not_3_out, not_4_out, not_5_out;

  not not_1 (not_1_out, QD);
  not not_2 (not_2_out, QB);
  and and_1 (and_1_out, not_1_out, not_2_out, not_3_out);
  not not_3 (not_3_out, QA);
  not not_4 (not_4_out, QD);
  and and_2 (and_2_out, not_4_out, QC);
  and and_3 (and_3_out, QD, not_5_out);
  not not_5 (not_5_out, QC);
  or or_1 (x, and_1_out, and_2_out, and_3_out);
endmodule

module demo (
);

  wire clock_1_out, fankui_1_x;
  wire [3:0] digital_oscilloscope_1_p3;

  Clock clock_1 (.out(clock_1_out));
  // Digital_Oscilloscope digital_oscilloscope_1: pin names not known; wires that end beside it: clock_1_out, digital_oscilloscope_1_p3[1], digital_oscilloscope_1_p3[0]
  main main_1 (
    .CLK(clock_1_out), .CLR(1'b0), .LIN(1'b0), .D(1'b0), .C(1'b0), .B(1'b0), .S1(1'b0), .S0(1'b1), .A(1'b1),
    .RIN(fankui_1_x), .QD(digital_oscilloscope_1_p3[3]), .QC(digital_oscilloscope_1_p3[2]),
    .QB(digital_oscilloscope_1_p3[1]), .QA(digital_oscilloscope_1_p3[0]));
  fankui fankui_1 (
    .QD(digital_oscilloscope_1_p3[3]), .QC(digital_oscilloscope_1_p3[2]), .x(fankui_1_x),
    .QB(digital_oscilloscope_1_p3[1]), .QA(digital_oscilloscope_1_p3[0]));
  Hex_Digit_Display hex_digit_display_1 (.value(digital_oscilloscope_1_p3));  // open: dp
endmodule
