// Logisim project 2.circ as structural Verilog: 1 circuit, main circuit main
module main (
  input  C0,
  input  P0,
  input  G0,
  input  P1,
  input  G1,
  input  P2,
  input  G2,
  input  P3,
  input  G3,
  output C1,
  output C2,
  output C3,
  output C4
);

  wire and_1_out, and_2_out, and_3_out, and_4_out, and_5_out, and_6_out, and_7_out, and_8_out, and_9_out,
       and_10_out;

  or or_1 (C1, and_1_out, G0);
  and and_1 (and_1_out, C0, P0);
  or or_2 (C2, and_3_out, and_2_out, G1);
  and and_2 (and_2_out, G0, P1);
  and and_3 (and_3_out, C0, P0, P1);
  and and_4 (and_4_out, G0, P1, P2);
  and and_5 (and_5_out, C0, P0, P1, P2);
  or or_3 (C3, and_5_out, and_4_out, and_6_out, G2);
  and and_6 (and_6_out, G1, P2);
  and and_7 (and_7_out, C0, P0, P1, P2, P3);
  and and_8 (and_8_out, G0, P1, P2, P3);
  or or_4 (C4, and_7_out, and_8_out, and_9_out, and_10_out, G3);
  and and_9 (and_9_out, G1, P2, P3);
  and and_10 (and_10_out, G2, P3);
endmodule
