// Logisim project 3.circ as structural Verilog: 7 circuits, main circuit main
module main (
  input  C0,
  input  [15:0] A,
  input  [15:0] B,
  output [15:0] out_4,
  output out_5
);

  wire cla_1_gg, cla_1_pg, cla_2_gg, cla_2_pg, cla_3_gg, cla_3_pg, cla_4_gg, cla_4_pg, clu_1_c1, clu_1_c2,
       clu_1_c3;

  cla cla_1 (.A(A[3:0]), .C0(C0), .B(B[3:0]), .Gg(cla_1_gg), .Pg(cla_1_pg), .S(out_4[3:0]));  // open: C4
  cla cla_2 (.A(A[7:4]), .C0(clu_1_c1), .B(B[7:4]), .Gg(cla_2_gg), .Pg(cla_2_pg), .S(out_4[7:4]));  // open: C4
  cla cla_3 (.A(A[11:8]), .C0(clu_1_c2), .B(B[11:8]), .Gg(cla_3_gg), .Pg(cla_3_pg), .S(out_4[11:8]));  // open: C4
  cla cla_4 (.A(A[15:12]), .C0(clu_1_c3), .B(B[15:12]), .C4(out_5), .Gg(cla_4_gg), .Pg(cla_4_pg), .S(out_4[15:12]));
  CLU clu_1 (
    .C0(C0), .C3(clu_1_c3), .C2(clu_1_c2), .C1(clu_1_c1), .G4(cla_4_gg), .P4(cla_4_pg), .G3(cla_3_gg),
    .P3(cla_3_pg), .G2(cla_2_gg), .P2(cla_2_pg), .G1(cla_1_gg), .P1(cla_1_pg));  // open: C4
endmodule

module FA (
  input  Cin,
  input  A,
  input  B,
  output P,
  output G,
  output F
);

  wire xor_2_out;

  xor xor_1 (F, B, xor_2_out);
  xor xor_2 (xor_2_out, A, Cin);
  or or_1 (P, A, B);
  and and_1 (G, A, B);
endmodule

module CLU (
  input  C0,
  input  G4,
  input  P4,
  input  G3,
  input  P3,
  input  G2,
  input  P2,
  input  G1,
  input  P1,
  output C4,
  output C3,
  output C2,
  output C1
);

  wire and_1_out, and_2_out, and_3_out, and_4_out, and_5_out, and_6_out, and_7_out, and_8_out, and_9_out,
       and_10_out;

  and and_1 (and_1_out, P4, P3, G2);
  and and_2 (and_2_out, P4, G3);
  or or_1 (C4, and_2_out, and_1_out, and_3_out, and_4_out, G4);
  and and_3 (and_3_out, P4, P3, P2, G1);
  and and_4 (and_4_out, P4, P3, P2, P1, C0);
  and and_5 (and_5_out, P3, G2);
  or or_2 (C3, and_5_out, and_6_out, G3, and_7_out);
  and and_6 (and_6_out, P3, P2, G1);
  and and_7 (and_7_out, P3, P2, P1, C0);
  or or_3 (C2, G2, and_8_out, and_9_out);
  and and_8 (and_8_out, P2, G1);
  and and_9 (and_9_out, P2, P1, C0);
  or or_4 (C1, G1, and_10_out);
  and and_10 (and_10_out, P1, C0);
endmodule

module cla (
  input  [3:0] A,
  input  C0,
  input  [3:0] B,
  output C4,
  output [3:0] S,
  output Gg,
  output Pg
);

  wire and_1_out, and_2_out, and_3_out, and_4_out, and_6_out, and_7_out, and_8_out, nand_1_out, nand_2_out,
       nand_3_out, nand_4_out, nor_1_out, nor_2_out, nor_3_out, nor_4_out, not_1_out, not_2_out, not_3_out,
       not_4_out, not_5_out, not_6_out, or_1_out, or_2_out, or_3_out, or_4_out, or_5_out, or_6_out, or_7_out,
       or_8_out, or_9_out, or_10_out;

  nand nand_1 (nand_1_out, B[3], A[3]);
  nor nor_1 (nor_1_out, B[3], A[3]);
  nand nand_2 (nand_2_out, B[2], A[2]);
  nor nor_2 (nor_2_out, B[2], A[2]);
  nand nand_3 (nand_3_out, B[1], A[1]);
  nor nor_3 (nor_3_out, B[1], A[1]);
  nand nand_4 (nand_4_out, B[0], A[0]);
  nor nor_4 (nor_4_out, B[0], A[0]);
  not not_1 (not_1_out, C0);
  not not_2 (not_2_out, nor_1_out);
  or or_1 (or_1_out, ~nor_2_out, ~nand_1_out);  // OR_Gate
  or or_2 (or_2_out, ~nor_3_out, ~nand_1_out, ~nand_2_out);  // OR_Gate
  or or_3 (or_3_out, ~nor_4_out, ~nand_1_out, ~nand_2_out, ~nand_3_out);  // OR_Gate
  or or_4 (or_4_out, ~nand_1_out, ~nand_2_out, ~nand_3_out, ~nand_4_out, ~not_1_out);  // OR_Gate
  and and_1 (and_1_out, nand_1_out, ~nor_1_out);  // AND_Gate
  not not_3 (not_3_out, nor_2_out);
  or or_5 (or_5_out, ~nor_3_out, ~nand_2_out);  // OR_Gate
  or or_6 (or_6_out, ~nor_4_out, ~nand_2_out, ~nand_3_out);  // OR_Gate
  or or_7 (or_7_out, ~nand_2_out, ~nand_3_out, ~nand_4_out, ~not_1_out);  // OR_Gate
  and and_2 (and_2_out, nand_2_out, ~nor_2_out);  // AND_Gate
  not not_4 (not_4_out, nor_3_out);
  or or_8 (or_8_out, ~nor_4_out, ~nand_3_out);  // OR_Gate
  or or_9 (or_9_out, ~nand_3_out, ~nand_4_out, ~not_1_out);  // OR_Gate
  and and_3 (and_3_out, nand_3_out, ~nor_3_out);  // AND_Gate
  not not_5 (not_5_out, nor_4_out);
  or or_10 (or_10_out, ~nand_4_out, ~not_1_out);  // OR_Gate
  and and_4 (and_4_out, nand_4_out, ~nor_4_out);  // AND_Gate
  not not_6 (not_6_out, not_1_out);
  temp temp_1 (
    .G0(nand_4_out), .G1(nand_3_out), .G2(nand_2_out), .G3(nand_1_out), .P0(nor_4_out), .P1(nor_3_out),
    .P2(nor_2_out), .P3(nor_1_out), .Gg(Gg), .Pg(Pg));
  and and_5 (C4, not_2_out, or_1_out, or_2_out, or_3_out, or_4_out);
  and and_6 (and_6_out, not_3_out, or_5_out, or_6_out, or_7_out);
  and and_7 (and_7_out, not_4_out, or_8_out, or_9_out);
  and and_8 (and_8_out, not_5_out, or_10_out);
  xor xor_1 (S[3], and_1_out, and_6_out);
  xor xor_2 (S[2], and_2_out, and_7_out);
  xor xor_3 (S[1], and_3_out, and_8_out);
  xor xor_4 (S[0], and_4_out, not_6_out);
endmodule

module temp (
  input  G0,
  input  G1,
  input  G2,
  input  G3,
  input  P0,
  input  P1,
  input  P2,
  input  P3,
  output Gg,
  output Pg
);

  wire and_1_out, and_2_out, and_3_out;

  and and_1 (and_1_out, P3, G2);
  and and_2 (and_2_out, P3, P2, G1);
  and and_3 (and_3_out, P3, P2, P1, G0);
  and and_4 (Pg, P3, P2, P1, P0);
  or or_1 (Gg, G3, and_1_out, and_2_out, and_3_out);
endmodule

module CLA (
  input  C0,
  input  [3:0] B,
  input  [3:0] A,
  output C4,
  output Pg,
  output Gg,
  output [3:0] S
);

  wire clu_1_c1, clu_1_c2, clu_1_c3, fa_1_g, fa_1_p, fa_2_g, fa_2_p, fa_3_g, fa_3_p, fa_4_g, fa_4_p;

  temp temp_1 (
    .G0(fa_4_g), .G1(fa_3_g), .G2(fa_2_g), .G3(fa_1_g), .P0(fa_4_p), .P1(fa_3_p), .P2(fa_2_p), .P3(fa_1_p),
    .Gg(Gg), .Pg(Pg));
  FA fa_1 (.F(S[3]), .Cin(clu_1_c3), .P(fa_1_p), .G(fa_1_g), .A(A[3]), .B(B[3]));
  FA fa_2 (.F(S[2]), .Cin(clu_1_c2), .P(fa_2_p), .G(fa_2_g), .A(A[2]), .B(B[2]));
  FA fa_3 (.F(S[1]), .Cin(clu_1_c1), .P(fa_3_p), .G(fa_3_g), .A(A[1]), .B(B[1]));
  CLU clu_1 (
    .C0(C0), .C4(C4), .C3(clu_1_c3), .C2(clu_1_c2), .C1(clu_1_c1), .G4(fa_1_g), .P4(fa_1_p), .G3(fa_2_g),
    .P3(fa_2_p), .G2(fa_3_g), .P2(fa_3_p), .G1(fa_4_g), .P1(fa_4_p));
  FA fa_4 (.F(S[0]), .Cin(C0), .P(fa_4_p), .G(fa_4_g), .A(A[0]), .B(B[0]));
endmodule

module main1 (
  input  C0,
  input  [15:0] A,
  input  [15:0] B,
  output [15:0] out_4,
  output out_5
);

  wire cla_1_c4, cla_1_gg, cla_1_pg, cla_2_c4, cla_2_gg, cla_2_pg, cla_3_c4, cla_3_gg, cla_3_pg, cla_4_gg,
       cla_4_pg, clu_1_c1, clu_1_c2, clu_1_c3;

  CLA cla_1 (.C4(cla_1_c4), .Pg(cla_1_pg), .Gg(cla_1_gg), .A(A[3:0]), .C0(C0), .B(B[3:0]), .S(out_4[3:0]));
  CLA cla_2 (.C4(cla_2_c4), .Pg(cla_2_pg), .Gg(cla_2_gg), .A(A[7:4]), .C0(cla_1_c4), .B(B[7:4]), .S(out_4[7:4]));
  CLA cla_3 (.C4(cla_3_c4), .Pg(cla_3_pg), .Gg(cla_3_gg), .A(A[11:8]), .C0(cla_2_c4), .B(B[11:8]), .S(out_4[11:8]));
  CLA cla_4 (.C4(out_5), .Pg(cla_4_pg), .Gg(cla_4_gg), .A(A[15:12]), .C0(cla_3_c4), .B(B[15:12]), .S(out_4[15:12]));
  CLU clu_1 (
    .C0(C0), .C3(clu_1_c3), .C2(clu_1_c2), .C1(clu_1_c1), .G4(cla_1_gg), .P4(cla_1_pg), .G3(cla_2_gg),
    .P3(cla_2_pg), .G2(cla_3_gg), .P2(cla_3_pg), .G1(cla_4_gg), .P1(cla_4_pg));  // open: C4
endmodule
