// Logisim project 4.circ as structural Verilog
module _32 (
  input  Cin,
  input  [31:0] A,
  input  [31:0] B,
  output CF,
  output ZF,
  output [31:0] out_6,
  output Cout,
  output OF
);

  wire main1_1_out_5;

  main1 main1_1 (.C0(Cin), .A(A[15:0]), .B(B[15:0]), .out_4(out_6[15:0]), .out_5(main1_1_out_5));
  main1 main1_2 (.C0(main1_1_out_5), .A(A[31:16]), .B(B[31:16]), .out_4(out_6[31:16]), .out_5(Cout));
  xor xor_1 (OF, Cout, main1_1_out_5);
  xor xor_2 (CF, Cin, Cout);
  nor nor_1 (ZF, out_6[0], out_6[1], out_6[2], out_6[3], out_6[4], out_6[5], out_6[6], out_6[7], out_6[8], out_6[9], out_6[10], out_6[11], out_6[12], out_6[13], out_6[14], out_6[15], out_6[17], out_6[18], out_6[19], out_6[20], out_6[21], out_6[22], out_6[23], out_6[24], out_6[25], out_6[26], out_6[27], out_6[28], out_6[29], out_6[30], out_6[31], out_6[16]);
endmodule
