// Logisim project 4-CLU.circ as structural Verilog
module _4_CLU (
  input  G3,
  input  P3,
  input  G2,
  input  P2,
  input  G1,
  input  P1,
  input  G0,
  input  P0,
  input  C0,
  output C4,
  output C3,
  output C2,
  output C1
);

  wire and_1_out, and_2_out, and_3_out, and_4_out, and_5_out, and_6_out, and_7_out, and_8_out, and_9_out,
       and_10_out;

  and and_1 (and_1_out, P3, G2);
  and and_2 (and_2_out, P3, P2, G1);
  and and_3 (and_3_out, P3, P2, P1, G0);
  and and_4 (and_4_out, P3, P2, P1, P0, C0);
  and and_5 (and_5_out, P2, G1);
  and and_6 (and_6_out, P2, P1, G0);
  and and_7 (and_7_out, P2, P1, P0, C0);
  and and_8 (and_8_out, P1, G0);
  and and_9 (and_9_out, P1, P0, C0);
  and and_10 (and_10_out, P0, C0);
  or or_1 (C4, G3, and_1_out, and_2_out, and_3_out, and_4_out);
  or or_2 (C3, G2, and_5_out, and_6_out, and_7_out);
  or or_3 (C2, G1, and_8_out, and_9_out);
  or or_4 (C1, G0, and_10_out);
endmodule

module CLU_test (
  input  [7:0] in_1,
  input  in_2,
  output [3:0] out_3
);

  _4_CLU u_4_clu_1 (
    .G3(in_1[7]), .P3(in_1[6]), .G2(in_1[5]), .P2(in_1[4]), .G1(in_1[3]), .P1(in_1[2]), .G0(in_1[1]),
    .P0(in_1[0]), .C0(in_2), .C4(out_3[3]), .C3(out_3[2]), .C2(out_3[1]), .C1(out_3[0]));
endmodule

module _4_CLU_wout (
  input  G3,
  input  P3,
  input  G2,
  input  P2,
  input  G1,
  input  P1,
  input  G0,
  input  P0,
  input  C0,
  output C4,
  output C3,
  output C2,
  output C1,
  output Gs0,
  output Ps0
);

  wire and_1_out, and_2_out, and_3_out, and_4_out, and_5_out, and_6_out, and_7_out, and_8_out, and_9_out,
       and_10_out, and_11_out, and_12_out, and_13_out;

  and and_1 (and_1_out, P3, G2);
  and and_2 (and_2_out, P3, P2, G1);
  and and_3 (and_3_out, P3, P2, P1, G0);
  and and_4 (and_4_out, P3, P2, P1, P0, C0);
  and and_5 (and_5_out, P2, G1);
  and and_6 (and_6_out, P2, P1, G0);
  and and_7 (and_7_out, P2, P1, P0, C0);
  and and_8 (and_8_out, P1, G0);
  and and_9 (and_9_out, P1, P0, C0);
  and and_10 (and_10_out, P0, C0);
  and and_11 (and_11_out, G2, P3);
  and and_12 (and_12_out, G1, P3, P2);
  and and_13 (and_13_out, G0, P3, P2, P1);
  or or_1 (C4, G3, and_1_out, and_2_out, and_3_out, and_4_out);
  or or_2 (C3, G2, and_5_out, and_6_out, and_7_out);
  or or_3 (C2, G1, and_8_out, and_9_out);
  or or_4 (C1, G0, and_10_out);
  or or_5 (Gs0, G3, and_11_out, and_12_out, and_13_out);
  and and_14 (Ps0, P3, P2, P1, P0);
endmodule
