// Logisim project ALU.circ as structural Verilog
module SEXT (
  input  in_1,
  output [31:0] out_2
);


  assign out_2 = {32{in_1}};
endmodule

module ALUctr (
  input  [3:0] ALUctr,
  output [1:0] OPctr,
  output SIGctr,
  output SUBctr
);

  wire or_1_out;

  or or_1 (or_1_out, ALUctr[3], ~ALUctr[2]);  // OR_Gate
  and and_1 (OPctr[1], or_1_out, ALUctr[1]);
  not not_1 (SIGctr, ALUctr[0]);
  or or_2 (SUBctr, ALUctr[1], ALUctr[3]);
  and and_2 (OPctr[0], ~ALUctr[3], ALUctr[1]);  // AND_Gate
endmodule

module ZEXT (
  input  in,
  output [31:0] out
);


  assign out = {{31{1'b0}}, in};
endmodule

module ALU (
  input  [31:0] A,
  input  [31:0] B,
  input  [3:0] ALUctr,
  output Zero,
  output [31:0] Result
);

  wire aluctr_1_sigctr, aluctr_1_subctr, multiplexer_2_out, n32_adder_wf_1_cf, n32_adder_wf_1_of,
       n32_adder_wf_1_sf, xor_2_out;
  wire [1:0] aluctr_1_opctr;
  wire [31:0] n32_adder_wf_1_f, or_1_out, sext_1_out_2, xor_1_out, zext_1_out;

  SEXT sext_1 (.in_1(aluctr_1_subctr), .out_2(sext_1_out_2));
  assign xor_1_out = B ^ sext_1_out_2;  // XOR_Gate xor_1, 32 bits wide
  assign or_1_out = A | B;  // OR_Gate or_1, 32 bits wide
  // Probe on A
  // Probe on A
  // Probe on B
  // Probe on B
  _32_adder_wf u_32_adder_wf_1 (
    .B(A), .A(xor_1_out), .Cin(aluctr_1_subctr), .F(n32_adder_wf_1_f), .OF(n32_adder_wf_1_of),
    .SF(n32_adder_wf_1_sf), .ZF(Zero), .CF(n32_adder_wf_1_cf));
  xor xor_2 (xor_2_out, n32_adder_wf_1_of, n32_adder_wf_1_sf);
  Multiplexer #(.select(2), .width(32), .enable("false")) multiplexer_1 (
    .in0(n32_adder_wf_1_f), .in1(or_1_out), .in2(B), .in3(zext_1_out), .out(Result), .sel(aluctr_1_opctr));
  ALUctr aluctr_1 (.OPctr(aluctr_1_opctr), .SIGctr(aluctr_1_sigctr), .SUBctr(aluctr_1_subctr), .ALUctr(ALUctr));
  ZEXT zext_1 (.in(multiplexer_2_out), .out(zext_1_out));
  Multiplexer #(.enable("false")) multiplexer_2 (
    .in0(n32_adder_wf_1_cf), .in1(xor_2_out), .out(multiplexer_2_out), .sel(aluctr_1_sigctr));
  // Probe on Result
  // Probe on Result
endmodule
