// Logisim project Circuits.circ as structural Verilog
module RAM_Test (
  input  [11:0] in_1,
  input  [7:0] in_2,
  input  \输入使能 ,
  input  \片选 ,
  input  \输出使能 
);

  wire \复位按钮_out , \时钟信号_out ;
  wire [7:0] ram_1_data;

  Clock \u_时钟信号  (.out(\时钟信号_out ));
  Button \u_复位按钮  (.out(\复位按钮_out ));
  RAM #(.addrWidth(12), .bus("separate"), .Select("low")) ram_1 (
    .addr(in_1), .din(in_2), .data(ram_1_data), .str(\输入使能 ), .sel(\片选 ), .clk(\时钟信号_out ), .ld(\输出使能 ),
    .clr(\复位按钮_out ));
  TTY tty_1 (.data(ram_1_data[6:0]), .clk(\时钟信号_out ), .clr(\复位按钮_out ));  // open: we
endmodule
