// Logisim project Lab5.circ as structural Verilog
module main (
  input  Jump,
  input  Branch,
  input  [2:0] ExtOp,
  input  [3:0] ALUctr,
  input  [1:0] in_5,
  input  ALUASrc,
  input  RegWR,
  input  MemWr,
  output [31:0] Instr,
  output [6:0] op,
  output [2:0] funct3,
  output [6:0] funct7,
  output [31:0] Imm
);

  wire ALU_p4, and_1_out, button_1_out, Clk_out, or_1_out;
  wire [4:0] \指令分解_1_out_5 , \指令分解_1_out_7 , \指令分解_1_out_8 ;
  wire [31:0] ALU_p5, multiplexer_1_out, multiplexer_2_out, multiplexer_3_out, n3_1_busa, n3_1_busb,
       n32_bit_signalcla_1_out_6, \n32_bit数据存储器_1_d , PC_q;

  Clock Clk (.out(Clk_out));
  Button button_1 (.out(button_1_out));
  Register #(.width(32), .Select("low")) PC (
    .D(n32_bit_signalcla_1_out_6), .Q(PC_q), .clk(Clk_out), .clr(button_1_out));  // open: en
  Multiplexer #(.width(32), .enable("false")) multiplexer_1 (
    .in0(32'h4), .in1(Imm), .out(multiplexer_1_out), .sel(or_1_out));
  or or_1 (or_1_out, Jump, and_1_out);
  and and_1 (and_1_out, Branch, ALU_p4);
  Multiplexer #(.select(2), .width(32), .enable("false")) multiplexer_2 (
    .in0(n3_1_busb), .in1(32'h4), .in2(Imm), .in3({32{1'b0}}), .out(multiplexer_2_out), .sel(in_5));
  _32_bit_SignalCLA u_32_bit_signalcla_1 (
    .C0(1'b0), .A(PC_q), .B(multiplexer_1_out), .out_6(n32_bit_signalcla_1_out_6));  // open: ZF, CF, OF, SF
  Multiplexer #(.width(32), .enable("false")) multiplexer_3 (
    .in0(n3_1_busa), .in1(PC_q), .out(multiplexer_3_out), .sel(ALUASrc));
  // ALU ALU: pin names not known; wires that end beside it: multiplexer_3_out, multiplexer_2_out, ALUctr, ALU_p4, ALU_p5
  RAM #(.addrWidth(12), .dataWidth(32), .Select("low")) ram_1 (
    .addr(PC_q[13:2]), .data(Instr), .clk(Clk_out), .clr(button_1_out));  // open: sel, ld
  \指令分解  \u_指令分解_1  (
    .\输入指令 (Instr), .ExtOp(ExtOp), .out_4(op), .out_5(\指令分解_1_out_5 ), .out_6(funct3),
    .out_7(\指令分解_1_out_7 ), .out_8(\指令分解_1_out_8 ), .out_9(funct7), .Imm(Imm));
  _3 u_3_1 (
    .RW(\指令分解_1_out_5 ), .busW(\n32_bit数据存储器_1_d ), .busA(n3_1_busa), .busB(n3_1_busb), .RA(\指令分解_1_out_7 ),
    .RB(\指令分解_1_out_8 ), .CLK(Clk_out), .WE(RegWR));
  \_32_bit数据存储器  \u_32_bit数据存储器_1  (
    .Address(ALU_p5), .Data_In(n3_1_busb), .Clk(Clk_out), .WriteEnable(MemWr), .D(\n32_bit数据存储器_1_d ));
endmodule

module RAM_Test (
  input  [11:0] in_1,
  input  [7:0] in_2,
  input  \输入使能 ,
  input  \片选 ,
  input  \输出使能 
);

  wire \复位按钮_out , \时钟信号_out ;
  wire [7:0] ram_1_data;

  Clock \u_时钟信号  (.out(\时钟信号_out ));
  Button \u_复位按钮  (.out(\复位按钮_out ));
  RAM #(.addrWidth(12), .bus("separate"), .Select("low")) ram_1 (
    .addr(in_1), .din(in_2), .data(ram_1_data), .str(\输入使能 ), .sel(\片选 ), .clk(\时钟信号_out ), .ld(\输出使能 ),
    .clr(\复位按钮_out ));
  TTY tty_1 (.data(ram_1_data[6:0]), .clk(\时钟信号_out ), .clr(\复位按钮_out ));  // open: we
endmodule

module _2 (
  input  [31:0] Imm,
  input  Jump,
  input  [2:0] in_3,
  input  Branch,
  input  Zero,
  output [31:0] Instr,
  output [6:0] op,
  output [4:0] Rd,
  output [2:0] funct3,
  output [4:0] Rs1,
  output [4:0] Rs2,
  output [6:0] funct7,
  output [31:0] Imm_2
);

  wire and_1_out, button_1_out, Clk_out, or_1_out;
  wire [31:0] multiplexer_1_out, n32_bit_signalcla_1_out_6, PC_q;

  Clock Clk (.out(Clk_out));
  Button button_1 (.out(button_1_out));
  Register #(.width(32), .Select("low")) PC (
    .D(n32_bit_signalcla_1_out_6), .Q(PC_q), .clk(Clk_out), .clr(button_1_out));  // open: en
  Multiplexer #(.width(32), .enable("false")) multiplexer_1 (
    .in0(32'h4), .in1(Imm), .out(multiplexer_1_out), .sel(or_1_out));
  or or_1 (or_1_out, Jump, and_1_out);
  and and_1 (and_1_out, Branch, Zero);
  _32_bit_SignalCLA u_32_bit_signalcla_1 (
    .C0(1'b0), .A(PC_q), .B(multiplexer_1_out), .out_6(n32_bit_signalcla_1_out_6));  // open: ZF, CF, OF, SF
  ROM #(.addrWidth(12), .dataWidth(32), .Select("low")) \u_指令存储器  (.addr(PC_q[13:2]), .data(Instr));
  \指令分解  \u_指令分解_1  (
    .\输入指令 (Instr), .ExtOp(in_3), .out_4(op), .out_5(Rd), .out_6(funct3), .out_7(Rs1), .out_8(Rs2),
    .out_9(funct7), .Imm(Imm_2));

  // Notes on the sheet:
  //   contents of 指令存储器 (hex, n*v repeats v):
  //   102*0 10010 10110111 11111111 11110010 10000010 10010011 101 11011110 11000 1100011 101000 10000000
  //   0 11101111 0 10001 100110 100011
endmodule

module \指令分解  (
  input  [31:0] \输入指令 ,
  input  [2:0] ExtOp,
  output [31:0] Imm,
  output [6:0] out_4,
  output [4:0] out_5,
  output [2:0] out_6,
  output [4:0] out_7,
  output [4:0] out_8,
  output [6:0] out_9
);

  InstrTolmm instrtolmm_1 (.Instr(\输入指令 ), .Extop(ExtOp), .imm(Imm));

  assign out_4 = \输入指令 [6:0];
  assign out_5 = \输入指令 [11:7];
  assign out_6 = \输入指令 [14:12];
  assign out_7 = \输入指令 [19:15];
  assign out_8 = \输入指令 [24:20];
  assign out_9 = \输入指令 [31:25];

  // Other names for the same wires on the sheet: op[6:0] = \输入指令 [6:0]; Rd[4:0] = \输入指令 [11:7];
  //   funct3[2:0] = \输入指令 [14:12]; Rs1[4:0] = \输入指令 [19:15]; Rs2[4:0] = \输入指令 [24:20]; funct7[6:0] = \输入指令 [31:25]
endmodule

module InstrTolmm (
  input  [31:0] Instr,
  input  [2:0] Extop,
  output [31:0] imm
);

  wire [11:0] bit_extender_4_out;
  wire [19:0] bit_extender_1_out, bit_extender_2_out, bit_extender_3_out;

  assign bit_extender_1_out = {{19{Instr[31]}}, Instr[31]};  // Bit_Extender bit_extender_1
  assign bit_extender_2_out = {{19{Instr[31]}}, Instr[31]};  // Bit_Extender bit_extender_2
  assign bit_extender_3_out = {{19{Instr[31]}}, Instr[31]};  // Bit_Extender bit_extender_3
  assign bit_extender_4_out = {{11{Instr[31]}}, Instr[31]};  // Bit_Extender bit_extender_4
  Multiplexer #(.select(3), .width(32), .enable("false")) multiplexer_1 (
    .in0({bit_extender_1_out, Instr[31:20]}), .in1({Instr[31:12], {12{1'b0}}}),
    .in2({bit_extender_2_out, Instr[31:25], Instr[11:7]}),
    .in3({bit_extender_3_out, Instr[7], Instr[30:25], Instr[11:8], 1'b0}),
    .in4({bit_extender_4_out, Instr[19:12], Instr[31:21], 1'b0}), .in5({32{1'b0}}), .in6({32{1'b0}}),
    .in7({32{1'b0}}), .out(imm), .sel(Extop));

  // Notes on the sheet:
  //   I
  //   U
  //   S
  //   B
  //   J
endmodule

module _32_32_bit_Registers (
  input  [4:0] Rs1,
  input  [4:0] Rs2,
  input  [4:0] RW,
  input  [31:0] busW,
  input  WE,
  input  CLK,
  output [31:0] busA,
  output [31:0] busB
);

  wire and_1_out, and_2_out, and_3_out, and_4_out, and_5_out, and_6_out, and_7_out, and_8_out, and_9_out,
       and_10_out, and_11_out, and_12_out, and_13_out, and_14_out, and_15_out, and_16_out, and_17_out,
       and_18_out, and_19_out, and_20_out, and_21_out, and_22_out, and_23_out, and_24_out, and_25_out,
       and_26_out, and_27_out, and_28_out, and_29_out, and_30_out, and_31_out, and_32_out, decoder_1_out0,
       decoder_1_out1, decoder_1_out2, decoder_1_out3, decoder_1_out4, decoder_1_out5, decoder_1_out6,
       decoder_1_out7, decoder_1_out8, decoder_1_out9, decoder_1_out10, decoder_1_out11, decoder_1_out12,
       decoder_1_out13, decoder_1_out14, decoder_1_out15, decoder_1_out16, decoder_1_out17, decoder_1_out18,
       decoder_1_out19, decoder_1_out20, decoder_1_out21, decoder_1_out22, decoder_1_out23, decoder_1_out24,
       decoder_1_out25, decoder_1_out26, decoder_1_out27, decoder_1_out28, decoder_1_out29, decoder_1_out30,
       decoder_1_out31;
  wire [31:0] register_1_q, register_2_q, register_3_q, register_4_q, register_5_q, register_6_q,
       register_7_q, register_8_q, register_9_q, register_10_q, register_11_q, register_12_q, register_13_q,
       register_14_q, register_15_q, register_16_q, register_17_q, register_18_q, register_19_q,
       register_20_q, register_21_q, register_22_q, register_23_q, register_24_q, register_25_q,
       register_26_q, register_27_q, register_28_q, register_29_q, register_30_q, register_31_q,
       register_32_q;

  Decoder #(.select(5), .enable("false")) decoder_1 (
    .out0(decoder_1_out0), .out1(decoder_1_out1), .out2(decoder_1_out2), .out3(decoder_1_out3),
    .out4(decoder_1_out4), .out5(decoder_1_out5), .out6(decoder_1_out6), .out7(decoder_1_out7),
    .out8(decoder_1_out8), .out9(decoder_1_out9), .out10(decoder_1_out10), .out11(decoder_1_out11),
    .out12(decoder_1_out12), .out13(decoder_1_out13), .out14(decoder_1_out14), .out15(decoder_1_out15),
    .out16(decoder_1_out16), .out17(decoder_1_out17), .out18(decoder_1_out18), .out19(decoder_1_out19),
    .out20(decoder_1_out20), .out21(decoder_1_out21), .out22(decoder_1_out22), .out23(decoder_1_out23),
    .out24(decoder_1_out24), .out25(decoder_1_out25), .out26(decoder_1_out26), .out27(decoder_1_out27),
    .out28(decoder_1_out28), .out29(decoder_1_out29), .out30(decoder_1_out30), .out31(decoder_1_out31),
    .sel(RW));
  and and_1 (and_1_out, CLK, WE, decoder_1_out0);
  and and_2 (and_2_out, CLK, WE, decoder_1_out1);
  and and_3 (and_3_out, CLK, WE, decoder_1_out2);
  and and_4 (and_4_out, CLK, WE, decoder_1_out3);
  and and_5 (and_5_out, CLK, WE, decoder_1_out4);
  and and_6 (and_6_out, CLK, WE, decoder_1_out5);
  and and_7 (and_7_out, CLK, WE, decoder_1_out6);
  and and_8 (and_8_out, CLK, WE, decoder_1_out7);
  and and_9 (and_9_out, CLK, WE, decoder_1_out8);
  and and_10 (and_10_out, CLK, WE, decoder_1_out9);
  and and_11 (and_11_out, CLK, WE, decoder_1_out10);
  and and_12 (and_12_out, CLK, WE, decoder_1_out11);
  and and_13 (and_13_out, CLK, WE, decoder_1_out12);
  and and_14 (and_14_out, CLK, WE, decoder_1_out13);
  and and_15 (and_15_out, CLK, WE, decoder_1_out14);
  and and_16 (and_16_out, CLK, WE, decoder_1_out15);
  and and_17 (and_17_out, CLK, WE, decoder_1_out16);
  and and_18 (and_18_out, CLK, WE, decoder_1_out17);
  and and_19 (and_19_out, CLK, WE, decoder_1_out18);
  and and_20 (and_20_out, CLK, WE, decoder_1_out19);
  and and_21 (and_21_out, CLK, WE, decoder_1_out20);
  and and_22 (and_22_out, CLK, WE, decoder_1_out21);
  and and_23 (and_23_out, CLK, WE, decoder_1_out22);
  and and_24 (and_24_out, CLK, WE, decoder_1_out23);
  and and_25 (and_25_out, CLK, WE, decoder_1_out24);
  and and_26 (and_26_out, CLK, WE, decoder_1_out25);
  and and_27 (and_27_out, CLK, WE, decoder_1_out26);
  and and_28 (and_28_out, CLK, WE, decoder_1_out27);
  and and_29 (and_29_out, CLK, WE, decoder_1_out28);
  and and_30 (and_30_out, CLK, WE, decoder_1_out29);
  and and_31 (and_31_out, CLK, WE, decoder_1_out30);
  and and_32 (and_32_out, CLK, WE, decoder_1_out31);
  Register #(.width(32), .Select("low")) register_1 (.D(busW), .Q(register_1_q), .clk(and_1_out));  // open: en, clr
  Register #(.width(32), .Select("low")) register_2 (.D(busW), .Q(register_2_q), .clk(and_2_out));  // open: en, clr
  Register #(.width(32), .Select("low")) register_3 (.D(busW), .Q(register_3_q), .clk(and_3_out));  // open: en, clr
  Register #(.width(32), .Select("low")) register_4 (.D(busW), .Q(register_4_q), .clk(and_4_out));  // open: en, clr
  Register #(.width(32), .Select("low")) register_5 (.D(busW), .Q(register_5_q), .clk(and_5_out));  // open: en, clr
  Register #(.width(32), .Select("low")) register_6 (.D(busW), .Q(register_6_q), .clk(and_6_out));  // open: en, clr
  Register #(.width(32), .Select("low")) register_7 (.D(busW), .Q(register_7_q), .clk(and_7_out));  // open: en, clr
  Register #(.width(32), .Select("low")) register_8 (.D(busW), .Q(register_8_q), .clk(and_8_out));  // open: en, clr
  Register #(.width(32), .Select("low")) register_9 (.D(busW), .Q(register_9_q), .clk(and_9_out));  // open: en, clr
  Register #(.width(32), .Select("low")) register_10 (.D(busW), .Q(register_10_q), .clk(and_10_out));  // open: en, clr
  Register #(.width(32), .Select("low")) register_11 (.D(busW), .Q(register_11_q), .clk(and_11_out));  // open: en, clr
  Register #(.width(32), .Select("low")) register_12 (.D(busW), .Q(register_12_q), .clk(and_12_out));  // open: en, clr
  Register #(.width(32), .Select("low")) register_13 (.D(busW), .Q(register_13_q), .clk(and_13_out));  // open: en, clr
  Register #(.width(32), .Select("low")) register_14 (.D(busW), .Q(register_14_q), .clk(and_14_out));  // open: en, clr
  Register #(.width(32), .Select("low")) register_15 (.D(busW), .Q(register_15_q), .clk(and_15_out));  // open: en, clr
  Register #(.width(32), .Select("low")) register_16 (.D(busW), .Q(register_16_q), .clk(and_16_out));  // open: en, clr
  Register #(.width(32), .Select("low")) register_17 (.D(busW), .Q(register_17_q), .clk(and_17_out));  // open: en, clr
  Register #(.width(32), .Select("low")) register_18 (.D(busW), .Q(register_18_q), .clk(and_18_out));  // open: en, clr
  Register #(.width(32), .Select("low")) register_19 (.D(busW), .Q(register_19_q), .clk(and_19_out));  // open: en, clr
  Register #(.width(32), .Select("low")) register_20 (.D(busW), .Q(register_20_q), .clk(and_20_out));  // open: en, clr
  Register #(.width(32), .Select("low")) register_21 (.D(busW), .Q(register_21_q), .clk(and_21_out));  // open: en, clr
  Register #(.width(32), .Select("low")) register_22 (.D(busW), .Q(register_22_q), .clk(and_22_out));  // open: en, clr
  Register #(.width(32), .Select("low")) register_23 (.D(busW), .Q(register_23_q), .clk(and_23_out));  // open: en, clr
  Register #(.width(32), .Select("low")) register_24 (.D(busW), .Q(register_24_q), .clk(and_24_out));  // open: en, clr
  Register #(.width(32), .Select("low")) register_25 (.D(busW), .Q(register_25_q), .clk(and_25_out));  // open: en, clr
  Register #(.width(32), .Select("low")) register_26 (.D(busW), .Q(register_26_q), .clk(and_26_out));  // open: en, clr
  Register #(.width(32), .Select("low")) register_27 (.D(busW), .Q(register_27_q), .clk(and_27_out));  // open: en, clr
  Register #(.width(32), .Select("low")) register_28 (.D(busW), .Q(register_28_q), .clk(and_28_out));  // open: en, clr
  Register #(.width(32), .Select("low")) register_29 (.D(busW), .Q(register_29_q), .clk(and_29_out));  // open: en, clr
  Register #(.width(32), .Select("low")) register_30 (.D(busW), .Q(register_30_q), .clk(and_30_out));  // open: en, clr
  Register #(.width(32), .Select("low")) register_31 (.D(busW), .Q(register_31_q), .clk(and_31_out));  // open: en, clr
  Register #(.width(32), .Select("low")) register_32 (.D(busW), .Q(register_32_q), .clk(and_32_out));  // open: en, clr
  Multiplexer #(.select(5), .width(32), .enable("false")) multiplexer_1 (
    .in0(register_1_q), .in1(register_2_q), .in2(register_3_q), .in3(register_4_q), .in4(register_5_q),
    .in5(register_6_q), .in6(register_7_q), .in7(register_8_q), .in8(register_9_q), .in9(register_10_q),
    .in10(register_11_q), .in11(register_12_q), .in12(register_13_q), .in13(register_14_q),
    .in14(register_15_q), .in15(register_16_q), .in16(register_17_q), .in17(register_18_q),
    .in18(register_19_q), .in19(register_20_q), .in20(register_21_q), .in21(register_22_q),
    .in22(register_23_q), .in23(register_24_q), .in24(register_25_q), .in25(register_26_q),
    .in26(register_27_q), .in27(register_28_q), .in28(register_29_q), .in29(register_30_q),
    .in30(register_31_q), .in31(register_32_q));  // open: out, sel
  Multiplexer #(.select(5), .width(32), .enable("false")) multiplexer_2 (
    .in0(register_1_q), .in1(register_2_q), .in2(register_3_q), .in3(register_4_q), .in4(register_5_q),
    .in5(register_6_q), .in6(register_7_q), .in7(register_8_q), .in8(register_9_q), .in9(register_10_q),
    .in10(register_11_q), .in11(register_12_q), .in12(register_13_q), .in13(register_14_q),
    .in14(register_15_q), .in15(register_16_q), .in16(register_17_q), .in17(register_18_q),
    .in18(register_19_q), .in19(register_20_q), .in20(register_21_q), .in21(register_22_q),
    .in22(register_23_q), .in23(register_24_q), .in24(register_25_q), .in25(register_26_q),
    .in26(register_27_q), .in27(register_28_q), .in28(register_29_q), .in29(register_30_q),
    .in30(register_31_q), .in31(register_32_q), .out(busA), .sel(Rs1));
  Multiplexer #(.select(5), .width(32), .enable("false")) multiplexer_3 (
    .in0(register_1_q), .in1(register_2_q), .in2(register_3_q), .in3(register_4_q), .in4(register_5_q),
    .in5(register_6_q), .in6(register_7_q), .in7(register_8_q), .in8(register_9_q), .in9(register_10_q),
    .in10(register_11_q), .in11(register_12_q), .in12(register_13_q), .in13(register_14_q),
    .in14(register_15_q), .in15(register_16_q), .in16(register_17_q), .in17(register_18_q),
    .in18(register_19_q), .in19(register_20_q), .in20(register_21_q), .in21(register_22_q),
    .in22(register_23_q), .in23(register_24_q), .in24(register_25_q), .in25(register_26_q),
    .in26(register_27_q), .in27(register_28_q), .in28(register_29_q), .in29(register_30_q),
    .in30(register_31_q), .in31(register_32_q), .out(busB), .sel(Rs2));
endmodule

module \_25_bit数据存储器  (
  input  [24:0] Address,
  input  [31:0] Data_In,
  input  Clk,
  input  WrEn,
  output [31:0] D
);

  wire [23:0] demultiplexer_1_out0, demultiplexer_1_out1;
  wire [31:0] ram_1_data, ram_2_data;

  Demultiplexer #(.width(24), .enable("false")) demultiplexer_1 (
    .out0(demultiplexer_1_out0), .out1(demultiplexer_1_out1), .in(Address[23:0]), .sel(Address[24]));
  RAM #(.addrWidth(24), .dataWidth(32), .bus("separate"), .Select("low")) ram_1 (
    .addr(demultiplexer_1_out0), .din(Data_In), .data(ram_1_data), .str(1'b1), .clk(Clk), .ld(WrEn));  // open: sel, clr
  RAM #(.addrWidth(24), .dataWidth(32), .bus("separate"), .Select("low")) ram_2 (
    .addr(demultiplexer_1_out1), .din(Data_In), .data(ram_2_data), .str(1'b1), .clk(Clk), .ld(WrEn));  // open: sel, clr
  Multiplexer #(.width(32), .enable("false")) multiplexer_1 (
    .in0(ram_1_data), .in1(ram_2_data), .out(D), .sel(Address[24]));
endmodule

module \_26_bit数据存储器  (
  input  [25:0] Address,
  input  [31:0] Data_In,
  input  Clk,
  input  WriteEnable,
  output [31:0] D
);

  wire [24:0] demultiplexer_1_out0, demultiplexer_1_out1;
  wire [31:0] \n25_bit数据存储器_1_d , \n25_bit数据存储器_2_d ;

  Demultiplexer #(.width(25), .enable("false")) demultiplexer_1 (
    .out0(demultiplexer_1_out0), .out1(demultiplexer_1_out1), .in(Address[24:0]), .sel(Address[25]));
  \_25_bit数据存储器  \u_25_bit数据存储器_1  (
    .Address(demultiplexer_1_out0), .Data_In(Data_In), .Clk(Clk), .WrEn(WriteEnable), .D(\n25_bit数据存储器_1_d ));
  \_25_bit数据存储器  \u_25_bit数据存储器_2  (
    .Address(demultiplexer_1_out1), .Data_In(Data_In), .Clk(Clk), .WrEn(WriteEnable), .D(\n25_bit数据存储器_2_d ));
  Multiplexer #(.width(32), .enable("false")) multiplexer_1 (
    .in0(\n25_bit数据存储器_1_d ), .in1(\n25_bit数据存储器_2_d ), .out(D), .sel(Address[25]));
endmodule

module \_27_bit数据存储器  (
  input  [26:0] Address,
  input  [31:0] Data_In,
  input  Clk,
  input  WriteEnable,
  output [31:0] D
);

  wire [25:0] demultiplexer_1_out0, demultiplexer_1_out1;
  wire [31:0] \n26_bit数据存储器_1_d , \n26_bit数据存储器_2_d ;

  Demultiplexer #(.width(26), .enable("false")) demultiplexer_1 (
    .out0(demultiplexer_1_out0), .out1(demultiplexer_1_out1), .in(Address[25:0]), .sel(Address[26]));
  \_26_bit数据存储器  \u_26_bit数据存储器_1  (
    .Address(demultiplexer_1_out0), .Data_In(Data_In), .Clk(Clk), .WriteEnable(WriteEnable),
    .D(\n26_bit数据存储器_1_d ));
  \_26_bit数据存储器  \u_26_bit数据存储器_2  (
    .Address(demultiplexer_1_out1), .Data_In(Data_In), .Clk(Clk), .WriteEnable(WriteEnable),
    .D(\n26_bit数据存储器_2_d ));
  Multiplexer #(.width(32), .enable("false")) multiplexer_1 (
    .in0(\n26_bit数据存储器_1_d ), .in1(\n26_bit数据存储器_2_d ), .out(D), .sel(Address[26]));
endmodule

module \_28_bit数据存储器  (
  input  [27:0] Address,
  input  [31:0] Data_In,
  input  Clk,
  input  WriteEnable,
  output [31:0] D
);

  wire [26:0] demultiplexer_1_out0, demultiplexer_1_out1;
  wire [31:0] \n27_bit数据存储器_1_d , \n27_bit数据存储器_2_d ;

  Demultiplexer #(.width(27), .enable("false")) demultiplexer_1 (
    .out0(demultiplexer_1_out0), .out1(demultiplexer_1_out1), .in(Address[26:0]), .sel(Address[27]));
  \_27_bit数据存储器  \u_27_bit数据存储器_1  (
    .Address(demultiplexer_1_out0), .Data_In(Data_In), .Clk(Clk), .WriteEnable(WriteEnable),
    .D(\n27_bit数据存储器_1_d ));
  \_27_bit数据存储器  \u_27_bit数据存储器_2  (
    .Address(demultiplexer_1_out1), .Data_In(Data_In), .Clk(Clk), .WriteEnable(WriteEnable),
    .D(\n27_bit数据存储器_2_d ));
  Multiplexer #(.width(32), .enable("false")) multiplexer_1 (
    .in0(\n27_bit数据存储器_1_d ), .in1(\n27_bit数据存储器_2_d ), .out(D), .sel(Address[27]));
endmodule

module \_29_bit数据存储器  (
  input  [28:0] Address,
  input  [31:0] Data_In,
  input  Clk,
  input  WriteEnable,
  output [31:0] D
);

  wire [27:0] demultiplexer_1_out0, demultiplexer_1_out1;
  wire [31:0] \n28_bit数据存储器_1_d , \n28_bit数据存储器_2_d ;

  Demultiplexer #(.width(28), .enable("false")) demultiplexer_1 (
    .out0(demultiplexer_1_out0), .out1(demultiplexer_1_out1), .in(Address[27:0]), .sel(Address[28]));
  \_28_bit数据存储器  \u_28_bit数据存储器_1  (
    .Address(demultiplexer_1_out0), .Data_In(Data_In), .Clk(Clk), .WriteEnable(WriteEnable),
    .D(\n28_bit数据存储器_1_d ));
  \_28_bit数据存储器  \u_28_bit数据存储器_2  (
    .Address(demultiplexer_1_out1), .Data_In(Data_In), .Clk(Clk), .WriteEnable(WriteEnable),
    .D(\n28_bit数据存储器_2_d ));
  Multiplexer #(.width(32), .enable("false")) multiplexer_1 (
    .in0(\n28_bit数据存储器_1_d ), .in1(\n28_bit数据存储器_2_d ), .out(D), .sel(Address[28]));
endmodule

module \_30_bit数据存储器  (
  input  [29:0] Address,
  input  [31:0] Data_In,
  input  Clk,
  input  WriteEnable,
  output [31:0] D
);

  wire [28:0] demultiplexer_1_out0, demultiplexer_1_out1;
  wire [31:0] \n29_bit数据存储器_1_d , \n29_bit数据存储器_2_d ;

  Demultiplexer #(.width(29), .enable("false")) demultiplexer_1 (
    .out0(demultiplexer_1_out0), .out1(demultiplexer_1_out1), .in(Address[28:0]), .sel(Address[29]));
  \_29_bit数据存储器  \u_29_bit数据存储器_1  (
    .Address(demultiplexer_1_out0), .Data_In(Data_In), .Clk(Clk), .WriteEnable(WriteEnable),
    .D(\n29_bit数据存储器_1_d ));
  \_29_bit数据存储器  \u_29_bit数据存储器_2  (
    .Address(demultiplexer_1_out1), .Data_In(Data_In), .Clk(Clk), .WriteEnable(WriteEnable),
    .D(\n29_bit数据存储器_2_d ));
  Multiplexer #(.width(32), .enable("false")) multiplexer_1 (
    .in0(\n29_bit数据存储器_1_d ), .in1(\n29_bit数据存储器_2_d ), .out(D), .sel(Address[29]));
endmodule

module \_31_bit数据存储器  (
  input  [30:0] Address,
  input  [31:0] Data_In,
  input  Clk,
  input  WriteEnable,
  output [31:0] D
);

  wire [29:0] demultiplexer_1_out0, demultiplexer_1_out1;
  wire [31:0] \n30_bit数据存储器_1_d , \n30_bit数据存储器_2_d ;

  Demultiplexer #(.width(30), .enable("false")) demultiplexer_1 (
    .out0(demultiplexer_1_out0), .out1(demultiplexer_1_out1), .in(Address[29:0]), .sel(Address[30]));
  \_30_bit数据存储器  \u_30_bit数据存储器_1  (
    .Address(demultiplexer_1_out0), .Data_In(Data_In), .Clk(Clk), .WriteEnable(WriteEnable),
    .D(\n30_bit数据存储器_1_d ));
  \_30_bit数据存储器  \u_30_bit数据存储器_2  (
    .Address(demultiplexer_1_out1), .Data_In(Data_In), .Clk(Clk), .WriteEnable(WriteEnable),
    .D(\n30_bit数据存储器_2_d ));
  Multiplexer #(.width(32), .enable("false")) multiplexer_1 (
    .in0(\n30_bit数据存储器_1_d ), .in1(\n30_bit数据存储器_2_d ), .out(D), .sel(Address[30]));
endmodule

module \_32_bit数据存储器  (
  input  [31:0] Address,
  input  [31:0] Data_In,
  input  Clk,
  input  WriteEnable,
  output [31:0] D
);

  wire [30:0] demultiplexer_1_out0, demultiplexer_1_out1;
  wire [31:0] \n31_bit数据存储器_1_d , \n31_bit数据存储器_2_d ;

  Demultiplexer #(.width(31), .enable("false")) demultiplexer_1 (
    .out0(demultiplexer_1_out0), .out1(demultiplexer_1_out1), .in(Address[30:0]), .sel(Address[31]));
  \_31_bit数据存储器  \u_31_bit数据存储器_1  (
    .Address(demultiplexer_1_out0), .Data_In(Data_In), .Clk(Clk), .WriteEnable(WriteEnable),
    .D(\n31_bit数据存储器_1_d ));
  \_31_bit数据存储器  \u_31_bit数据存储器_2  (
    .Address(demultiplexer_1_out1), .Data_In(Data_In), .Clk(Clk), .WriteEnable(WriteEnable),
    .D(\n31_bit数据存储器_2_d ));
  Multiplexer #(.width(32), .enable("false")) multiplexer_1 (
    .in0(\n31_bit数据存储器_1_d ), .in1(\n31_bit数据存储器_2_d ), .out(D), .sel(Address[31]));
endmodule
