// Logisim project 16-adder.circ as structural Verilog
module _4_adder (
  input  [3:0] B,
  input  [3:0] A,
  input  C0,
  output [3:0] S,
  output C4,
  output Gg,
  output Pg
);

  wire fa_1_g, fa_1_p, fa_2_g, fa_2_p, fa_3_g, fa_3_p, fa_4_g, fa_4_p, n4_clu_wout_1_c1, n4_clu_wout_1_c2,
       n4_clu_wout_1_c3;

  FA fa_1 (.B(B[3]), .A(A[3]), .Cin(n4_clu_wout_1_c3), .G(fa_1_g), .P(fa_1_p), .F(S[3]));
  FA fa_2 (.B(B[2]), .A(A[2]), .Cin(n4_clu_wout_1_c2), .G(fa_2_g), .P(fa_2_p), .F(S[2]));
  FA fa_3 (.B(B[1]), .A(A[1]), .Cin(n4_clu_wout_1_c1), .G(fa_3_g), .P(fa_3_p), .F(S[1]));
  FA fa_4 (.B(B[0]), .A(A[0]), .Cin(C0), .G(fa_4_g), .P(fa_4_p), .F(S[0]));
  _4_CLU_wout u_4_clu_wout_1 (
    .G3(fa_1_g), .P3(fa_1_p), .G2(fa_2_g), .P2(fa_2_p), .G1(fa_3_g), .P1(fa_3_p), .G0(fa_4_g), .P0(fa_4_p),
    .C0(C0), .C4(C4), .C3(n4_clu_wout_1_c3), .C2(n4_clu_wout_1_c2), .C1(n4_clu_wout_1_c1), .Gs0(Gg), .Ps0(Pg));
endmodule

module FA (
  input  B,
  input  A,
  input  Cin,
  output G,
  output P,
  output F
);

  wire and_2_out;

  and and_1 (G, B, A);
  or or_1 (P, B, A);
  and and_2 (and_2_out, ~G, P);  // AND_Gate
  xor xor_1 (F, and_2_out, Cin);
endmodule

module _16_adder (
  input  [15:0] B,
  input  [15:0] A,
  input  C0,
  output [15:0] S,
  output C16,
  output Gs0,
  output Ps0
);

  wire n4_adder_1_gg, n4_adder_1_pg, n4_adder_2_gg, n4_adder_2_pg, n4_adder_3_gg, n4_adder_3_pg,
       n4_adder_4_gg, n4_adder_4_pg, n4_clu_wout_1_c1, n4_clu_wout_1_c2, n4_clu_wout_1_c3;

  _4_adder u_4_adder_1 (
    .B(B[15:12]), .A(A[15:12]), .C0(n4_clu_wout_1_c3), .Pg(n4_adder_1_pg), .S(S[15:12]), .Gg(n4_adder_1_gg));  // open: C4
  _4_adder u_4_adder_2 (
    .B(B[11:8]), .A(A[11:8]), .C0(n4_clu_wout_1_c2), .Pg(n4_adder_2_pg), .S(S[11:8]), .Gg(n4_adder_2_gg));  // open: C4
  _4_adder u_4_adder_3 (
    .B(B[7:4]), .A(A[7:4]), .C0(n4_clu_wout_1_c1), .Pg(n4_adder_3_pg), .S(S[7:4]), .Gg(n4_adder_3_gg));  // open: C4
  _4_adder u_4_adder_4 (
    .B(B[3:0]), .A(A[3:0]), .C0(C0), .Pg(n4_adder_4_pg), .S(S[3:0]), .Gg(n4_adder_4_gg));  // open: C4
  _4_CLU_wout u_4_clu_wout_1 (
    .G3(n4_adder_1_gg), .P3(n4_adder_1_pg), .G2(n4_adder_2_gg), .P2(n4_adder_2_pg), .G1(n4_adder_3_gg),
    .P1(n4_adder_3_pg), .G0(n4_adder_4_gg), .P0(n4_adder_4_pg), .C0(C0), .C4(C16), .C3(n4_clu_wout_1_c3),
    .C2(n4_clu_wout_1_c2), .C1(n4_clu_wout_1_c1), .Gs0(Gs0), .Ps0(Ps0));
endmodule

module _16_adder_test (
  input  [15:0] A,
  input  [15:0] B,
  input  Cin,
  output [15:0] out_4,
  output out_5
);

  _16_adder u_16_adder_1 (.B(A), .A(B), .C0(Cin), .S(out_4), .C16(out_5));  // open: Gs0, Ps0
endmodule
