// Logisim project 32-adder.circ as structural Verilog
module _4_adder_wf (
  input  [3:0] B,
  input  [3:0] A,
  input  C0,
  output [3:0] S,
  output C4,
  output C3,
  output Gg,
  output Pg
);

  wire fa_1_g, fa_1_p, fa_2_g, fa_2_p, fa_3_g, fa_3_p, fa_4_g, fa_4_p, n4_clu_wout_1_c1, n4_clu_wout_1_c2;

  FA fa_1 (.B(B[3]), .A(A[3]), .Cin(C3), .G(fa_1_g), .P(fa_1_p), .F(S[3]));
  FA fa_2 (.B(B[2]), .A(A[2]), .Cin(n4_clu_wout_1_c2), .G(fa_2_g), .P(fa_2_p), .F(S[2]));
  FA fa_3 (.B(B[1]), .A(A[1]), .Cin(n4_clu_wout_1_c1), .G(fa_3_g), .P(fa_3_p), .F(S[1]));
  FA fa_4 (.B(B[0]), .A(A[0]), .Cin(C0), .G(fa_4_g), .P(fa_4_p), .F(S[0]));
  _4_CLU_wout u_4_clu_wout_1 (
    .G3(fa_1_g), .P3(fa_1_p), .G2(fa_2_g), .P2(fa_2_p), .G1(fa_3_g), .P1(fa_3_p), .G0(fa_4_g), .P0(fa_4_p),
    .C0(C0), .C4(C4), .C3(C3), .C2(n4_clu_wout_1_c2), .C1(n4_clu_wout_1_c1), .Gs0(Gg), .Ps0(Pg));
endmodule

module _16_adder_wf (
  input  [15:0] B,
  input  [15:0] A,
  input  C0,
  output [15:0] S,
  output C16,
  output C15,
  output Gs0,
  output Ps0
);

  wire n4_adder_1_gg, n4_adder_1_pg, n4_adder_2_gg, n4_adder_2_pg, n4_adder_3_gg, n4_adder_3_pg,
       n4_adder_wf_1_gg, n4_adder_wf_1_pg, n4_clu_wout_1_c1, n4_clu_wout_1_c2, n4_clu_wout_1_c3;

  _4_adder_wf u_4_adder_wf_1 (
    .B(B[15:12]), .A(A[15:12]), .C0(n4_clu_wout_1_c3), .Gg(n4_adder_wf_1_gg), .Pg(n4_adder_wf_1_pg),
    .S(S[15:12]), .C3(C15));  // open: C4
  _4_adder u_4_adder_1 (
    .B(B[11:8]), .A(A[11:8]), .C0(n4_clu_wout_1_c2), .Pg(n4_adder_1_pg), .S(S[11:8]), .Gg(n4_adder_1_gg));  // open: C4
  _4_adder u_4_adder_2 (
    .B(B[7:4]), .A(A[7:4]), .C0(n4_clu_wout_1_c1), .Pg(n4_adder_2_pg), .S(S[7:4]), .Gg(n4_adder_2_gg));  // open: C4
  _4_adder u_4_adder_3 (
    .B(B[3:0]), .A(A[3:0]), .C0(C0), .Pg(n4_adder_3_pg), .S(S[3:0]), .Gg(n4_adder_3_gg));  // open: C4
  _4_CLU_wout u_4_clu_wout_1 (
    .G3(n4_adder_wf_1_gg), .P3(n4_adder_wf_1_pg), .G2(n4_adder_1_gg), .P2(n4_adder_1_pg), .G1(n4_adder_2_gg),
    .P1(n4_adder_2_pg), .G0(n4_adder_3_gg), .P0(n4_adder_3_pg), .C0(C0), .C4(C16), .C3(n4_clu_wout_1_c3),
    .C2(n4_clu_wout_1_c2), .C1(n4_clu_wout_1_c1), .Gs0(Gs0), .Ps0(Ps0));
endmodule

module _32_adder_wf (
  input  [31:0] B,
  input  [31:0] A,
  input  Cin,
  output [31:0] F,
  output OF,
  output SF,
  output ZF,
  output CF
);

  wire and_1_out, n16_adder_1_gs0, n16_adder_1_ps0, n16_adder_wf_1_c15, n16_adder_wf_1_c16, or_1_out;

  _16_adder_wf u_16_adder_wf_1 (
    .B(B[31:16]), .A(A[31:16]), .C0(or_1_out), .S(F[31:16]), .C16(n16_adder_wf_1_c16),
    .C15(n16_adder_wf_1_c15));  // open: Gs0, Ps0
  _16_adder u_16_adder_1 (
    .B(B[15:0]), .A(A[15:0]), .C0(Cin), .Gs0(n16_adder_1_gs0), .Ps0(n16_adder_1_ps0), .S(F[15:0]));  // open: C16
  NOR_ALL nor_all_1 (.in(F), .out(ZF));
  or or_1 (or_1_out, n16_adder_1_gs0, and_1_out);
  and and_1 (and_1_out, n16_adder_1_ps0, Cin);
  xor xor_1 (OF, n16_adder_wf_1_c16, n16_adder_wf_1_c15);
  xor xor_2 (CF, n16_adder_wf_1_c16, Cin);

  assign SF = F[31];
endmodule

module NOR_ALL (
  input  [31:0] in,
  output out
);

  nor nor_1 (out, in[0], in[1], in[2], in[3], in[4], in[5], in[6], in[7], in[8], in[9], in[10], in[11], in[12], in[13], in[14], in[15], in[16], in[17], in[18], in[19], in[20], in[21], in[22], in[23], in[24], in[25], in[26], in[27], in[28], in[29], in[30], in[31]);
endmodule

module _32_adder_test (
  input  in_1,
  input  [31:0] in_2,
  input  [31:0] in_3,
  output out_4,
  output out_5,
  output out_6,
  output out_7,
  output [31:0] out_8
);

  _32_adder_wf u_32_adder_wf_1 (
    .B(in_2), .A(in_3), .Cin(in_1), .F(out_8), .OF(out_6), .SF(out_7), .ZF(out_5), .CF(out_4));
endmodule
