// Logisim project CPU.circ as structural Verilog
module CPU (
  output [2:0] ExtOp,
  output [6:0] op,
  output [31:0] out_3,
  output [31:0] imm,
  output [1:0] ALUBsrc,
  output [4:0] Rd,
  output ALUAsrc,
  output [3:0] ALUctr,
  output [2:0] funct3,
  output [31:0] out_10,
  output Jump,
  output [31:0] Instr,
  output [4:0] Rs1,
  output Branch,
  output [4:0] Rs2,
  output MemWr,
  output MemtoReg,
  output [6:0] funct7,
  output [31:0] out_19,
  output RegWr,
  output [31:0] PC,
  output [31:0] out_22
);

  wire and_1_out, and_2_out, and_3_out, Clk, not_1_out, not_2_out, or_1_out, Reset, Zero;
  wire [0:0] or_2_out;
  wire [31:0] adder_1_out, multiplexer_1_out, multiplexer_2_out, multiplexer_3_out, ram_1_data, undriven;

  Clock clock_1 (.out(Clk));
  Button button_1 (.out(Reset));
  not not_1 (not_1_out, Clk);
  and and_1 (and_1_out, Branch, Zero);
  or or_1 (or_1_out, and_1_out, Jump);
  _32_32Regfile u_32_32regfile_1 (
    .R1_num(Instr[19:15]), .R2_num(Instr[24:20]), .Write_Reg_num(Instr[11:7]), .Write_Enable(RegWr),
    .Clock(Clk), .Din(out_3), .Reg1Out(out_10), .Reg2Out(out_19), .Reset(Reset));
  Register #(.width(32), .Select("low")) u_PC (.D(adder_1_out), .Q(PC), .clk(not_1_out), .clr(Reset));  // open: en
  Multiplexer #(.width(32), .enable("false")) multiplexer_1 (
    .in0(32'h4), .in1(imm), .out(multiplexer_1_out), .sel(or_1_out));
  Adder #(.width(32)) adder_1 (.a(PC), .b(multiplexer_1_out), .out(adder_1_out));  // open: cin, cout
  ROM #(.addrWidth(24), .dataWidth(32), .Select("low")) rom_1 (
    .addr(PC[25:2]), .data({funct7, Instr[24:15], funct3, Instr[11:0]}));
  Multiplexer #(.width(32), .enable("false")) multiplexer_2 (
    .in0(out_10), .in1(PC), .out(multiplexer_2_out), .sel(ALUAsrc));
  Multiplexer #(.select(2), .width(32), .enable("false")) multiplexer_3 (
    .in0(out_19), .in1(32'h4), .in2(imm), .in3(undriven), .out(multiplexer_3_out), .sel(ALUBsrc));
  ALU alu_1 (.Zero(Zero), .Result(out_22), .A(multiplexer_2_out), .B(multiplexer_3_out), .ALUctr(ALUctr));
  InstrTolmm instrtolmm_1 (.Instr({funct7, Instr[24:15], funct3, Instr[11:0]}), .out_3(imm), .ExtOp(ExtOp));
  and and_2 (and_2_out, Instr[0], Instr[1], ~Instr[2], ~Instr[3], Instr[4], Instr[5], ~Instr[6]);  // AND_Gate
  and and_3 (and_3_out, Instr[0], Instr[1], ~Instr[2], ~Instr[3], Instr[4], ~Instr[5], ~Instr[6]);  // AND_Gate
  not not_2 (not_2_out, Clk);
  or or_2 (or_2_out[0], and_2_out, and_3_out);
  RAM #(.addrWidth(24), .dataWidth(32), .bus("separate"), .Select("low")) ram_1 (
    .addr(out_22[25:2]), .din(out_19), .data(ram_1_data), .str(MemWr), .clk(not_2_out), .clr(Reset));  // open: sel, ld
  // PlaRom #(.\and (10), .outputs(15), .Contents("0*3 1 2 2 1 1 2 2 0*4 1 1 2 1 1 2 2 0*4 1 2 2 1 2*3 0*4 1*5 2 2 0*4 1 2 1*3 2 2 0*4 2 2 1*3 2 2 0*4 2 2 1 2*4 0*3 2 0*7 2 0 2 0*8 2 2 0*9 2 1 0*14 1 0*9 1 0*4 1 0*4 1*4 0 1 0*3 1*3 0*8 1 0*6 1 0*7 1 0 0 1 0*4 1 0 1 0*7 1*3 0*3 1 0*4 1 0 1 1 0*10 1 0*13 1 0*13 1 0*8")) plarom_1: pin names not known; wires that end beside it: {funct3, Instr[6:0], or_2_out[0]}, {RegWr, MemtoReg, MemWr, Branch, Jump, ALUctr, ALUAsrc, ALUBsrc, ExtOp}
  Multiplexer #(.width(32), .enable("false")) multiplexer_4 (
    .in0(out_22), .in1(ram_1_data), .out(out_3), .sel(MemtoReg));

  assign {Instr[31:25], Instr[14:12]} = {funct7, funct3};
  assign op = Instr[6:0];
  assign Rd = Instr[11:7];
  assign Rs1 = Instr[19:15];
  assign Rs2 = Instr[24:20];

  // Other names for the same wires on the sheet: busA[31:0] = out_10; busB[31:0] = out_19; busW[31:0] = out_3;
  //   Result[31:0] = out_22

  // Notes on the sheet:
  //   contents of rom_1 (hex, n*v repeats v):
  //   2083 8133 106213 406293 fff06313 4410663 106193 406393 806413 21b5b3 2058063 3a483 42503 a4b5b3
  //   458c63 a3a023 942023 c0006f 610133 fc9ff06f 4181b3 5383b3 540433 fc9ff06f 6f
endmodule
