// Logisim project Circuits.circ as structural Verilog
module _4_bit_CLA (
  input  B3,
  input  A3,
  input  B2,
  input  A2,
  input  B1,
  input  A1,
  input  B0,
  input  A0,
  input  C0,
  output C4,
  output S3,
  output S2,
  output S1,
  output S0
);

  wire and_1_out, and_2_out, and_3_out, and_4_out, and_6_out, and_7_out, and_8_out, nand_1_out, nand_2_out,
       nand_3_out, nand_4_out, nor_1_out, nor_2_out, nor_3_out, nor_4_out, not_1_out, not_2_out, not_3_out,
       not_4_out, not_5_out, not_6_out, or_1_out, or_2_out, or_3_out, or_4_out, or_5_out, or_6_out, or_7_out,
       or_8_out, or_9_out, or_10_out;

  not not_1 (not_1_out, C0);
  nand nand_1 (nand_1_out, B3, A3);
  nor nor_1 (nor_1_out, B3, A3);
  nand nand_2 (nand_2_out, B2, A2);
  nor nor_2 (nor_2_out, B2, A2);
  nand nand_3 (nand_3_out, B1, A1);
  nor nor_3 (nor_3_out, B1, A1);
  nand nand_4 (nand_4_out, B0, A0);
  nor nor_4 (nor_4_out, B0, A0);
  not not_2 (not_2_out, nor_1_out);
  or or_1 (or_1_out, ~nor_2_out, ~nand_1_out);  // OR_Gate
  or or_2 (or_2_out, ~nor_3_out, ~nand_1_out, ~nand_2_out);  // OR_Gate
  or or_3 (or_3_out, ~nor_4_out, ~nand_1_out, ~nand_2_out, ~nand_3_out);  // OR_Gate
  or or_4 (or_4_out, ~nand_1_out, ~nand_2_out, ~nand_3_out, ~nand_4_out, ~not_1_out);  // OR_Gate
  and and_1 (and_1_out, nand_1_out, ~nor_1_out);  // AND_Gate
  not not_3 (not_3_out, nor_2_out);
  or or_5 (or_5_out, ~nor_3_out, ~nand_2_out);  // OR_Gate
  or or_6 (or_6_out, ~nor_4_out, ~nand_2_out, ~nand_3_out);  // OR_Gate
  or or_7 (or_7_out, ~nand_2_out, ~nand_3_out, ~nand_4_out, ~not_1_out);  // OR_Gate
  and and_2 (and_2_out, nand_2_out, ~nor_2_out);  // AND_Gate
  not not_4 (not_4_out, nor_3_out);
  or or_8 (or_8_out, ~nor_4_out, ~nand_3_out);  // OR_Gate
  or or_9 (or_9_out, ~nand_3_out, ~nand_4_out, ~not_1_out);  // OR_Gate
  and and_3 (and_3_out, nand_3_out, ~nor_3_out);  // AND_Gate
  not not_5 (not_5_out, nor_4_out);
  or or_10 (or_10_out, ~nand_4_out, ~not_1_out);  // OR_Gate
  and and_4 (and_4_out, nand_4_out, ~nor_4_out);  // AND_Gate
  not not_6 (not_6_out, not_1_out);
  and and_5 (C4, not_2_out, or_1_out, or_2_out, or_3_out, or_4_out);
  and and_6 (and_6_out, not_3_out, or_5_out, or_6_out, or_7_out);
  and and_7 (and_7_out, not_4_out, or_8_out, or_9_out);
  and and_8 (and_8_out, not_5_out, or_10_out);
  xor xor_1 (S3, and_1_out, and_6_out);
  xor xor_2 (S2, and_2_out, and_7_out);
  xor xor_3 (S1, and_3_out, and_8_out);
  xor xor_4 (S0, and_4_out, not_6_out);
endmodule

module _4_bit_CLU (
  input  C0,
  input  G4,
  input  P4,
  input  G3,
  input  P3,
  input  G2,
  input  P2,
  input  G1,
  input  P1,
  output C4,
  output C3,
  output C2,
  output C1
);

  wire and_1_out, and_2_out, and_3_out, and_4_out, and_5_out, and_6_out, and_7_out, and_8_out, and_9_out,
       and_10_out;

  and and_1 (and_1_out, P4, G3);
  and and_2 (and_2_out, P4, P3, G2);
  or or_1 (C4, G4, and_1_out, and_2_out, and_3_out, and_4_out);
  and and_3 (and_3_out, P4, P3, P2, G1);
  and and_4 (and_4_out, P4, P3, P2, P1, C0);
  or or_2 (C3, G3, and_5_out, and_6_out, and_7_out);
  and and_5 (and_5_out, P3, G2);
  and and_6 (and_6_out, P3, P2, G1);
  and and_7 (and_7_out, P3, P2, P1, C0);
  or or_3 (C2, G2, and_8_out, and_9_out);
  and and_8 (and_8_out, P2, G1);
  and and_9 (and_9_out, P2, P1, C0);
  or or_4 (C1, G1, and_10_out);
  and and_10 (and_10_out, P1, C0);
endmodule

module FullAdder (
  input  A,
  input  B,
  input  C,
  output G,
  output P,
  output F
);

  wire xor_1_out;

  and and_1 (G, A, B);
  or or_1 (P, A, B);
  xor xor_1 (xor_1_out, A, B);
  xor xor_2 (F, xor_1_out, C);
endmodule

module _4_bit_adder (
  input  [3:0] B,
  input  [3:0] A,
  input  C0,
  output Gg,
  output Pg,
  output C4,
  output [3:0] S,
  output F3,
  output C3
);

  wire FA0_g, FA0_p, FA1_g, FA1_p, FA2_g, FA2_p, FA3_g, FA3_p, n4_bit_clu_1_c1, n4_bit_clu_1_c2;

  FullAdder FA3 (.A(A[3]), .B(B[3]), .C(C3), .G(FA3_g), .P(FA3_p), .F(F3));
  FullAdder FA2 (.A(A[2]), .B(B[2]), .C(n4_bit_clu_1_c2), .G(FA2_g), .P(FA2_p), .F(S[2]));
  FullAdder FA1 (.A(A[1]), .B(B[1]), .C(n4_bit_clu_1_c1), .G(FA1_g), .P(FA1_p), .F(S[1]));
  FullAdder FA0 (.A(A[0]), .B(B[0]), .C(C0), .G(FA0_g), .P(FA0_p), .F(S[0]));
  _4_bit_CLU u_4_bit_clu_1 (
    .C0(C0), .C4(C4), .C3(C3), .C2(n4_bit_clu_1_c2), .C1(n4_bit_clu_1_c1), .G4(FA3_g), .P4(FA3_p),
    .G3(FA2_g), .P3(FA2_p), .G2(FA1_g), .P2(FA1_p), .G1(FA0_g), .P1(FA0_p));
  Feedback feedback_1 (
    .P0(FA0_p), .G0(FA0_g), .P1(FA1_p), .G1(FA1_g), .P2(FA2_p), .G2(FA2_g), .P3(FA3_p), .G3(FA3_g), .Gg(Gg),
    .Pg(Pg));

  assign S[3] = F3;
endmodule

module PGGenerator (
  input  A,
  input  B,
  output G,
  output P
);

  and and_1 (G, A, B);
  or or_1 (P, A, B);
endmodule

module Feedback (
  input  P0,
  input  G0,
  input  P1,
  input  G1,
  input  P2,
  input  G2,
  input  P3,
  input  G3,
  output Gg,
  output Pg
);

  wire and_1_out, and_2_out, and_3_out;

  and and_1 (and_1_out, P3, G2);
  and and_2 (and_2_out, P3, P2, G1);
  and and_3 (and_3_out, P3, P2, P1, G0);
  and and_4 (Pg, P3, P2, P1, P0);
  or or_1 (Gg, G3, and_1_out, and_2_out, and_3_out);
endmodule

module _16_bit_CLA (
  input  C0,
  input  [15:0] A,
  input  [15:0] B,
  output C4,
  output Cn_1,
  output [15:0] S,
  output Fn_1
);

  wire n4_bit_adder_1_gg, n4_bit_adder_1_pg, n4_bit_adder_2_gg, n4_bit_adder_2_pg, n4_bit_adder_3_gg,
       n4_bit_adder_3_pg, n4_bit_adder_4_gg, n4_bit_adder_4_pg, n4_bit_clu_1_c1, n4_bit_clu_1_c2,
       n4_bit_clu_1_c3;

  // Probe on A
  // Probe on B
  _4_bit_adder u_4_bit_adder_1 (
    .B(B[3:0]), .A(A[3:0]), .Gg(n4_bit_adder_1_gg), .Pg(n4_bit_adder_1_pg), .S(S[3:0]), .C0(C0));  // open: C4, C3, F3
  _4_bit_adder u_4_bit_adder_2 (
    .B(B[7:4]), .A(A[7:4]), .Gg(n4_bit_adder_2_gg), .Pg(n4_bit_adder_2_pg), .S(S[7:4]), .C0(n4_bit_clu_1_c1));  // open: C4, C3, F3
  _4_bit_adder u_4_bit_adder_3 (
    .B(B[11:8]), .A(A[11:8]), .Gg(n4_bit_adder_3_gg), .Pg(n4_bit_adder_3_pg), .S(S[11:8]),
    .C0(n4_bit_clu_1_c2));  // open: C4, C3, F3
  _4_bit_adder u_4_bit_adder_4 (
    .B(B[15:12]), .A(A[15:12]), .Gg(n4_bit_adder_4_gg), .Pg(n4_bit_adder_4_pg), .C4(C4), .S(S[15:12]),
    .C0(n4_bit_clu_1_c3), .C3(Cn_1), .F3(Fn_1));
  _4_bit_CLU u_4_bit_clu_1 (
    .C0(C0), .C3(n4_bit_clu_1_c3), .C2(n4_bit_clu_1_c2), .C1(n4_bit_clu_1_c1), .G4(n4_bit_adder_4_gg),
    .P4(n4_bit_adder_4_pg), .G3(n4_bit_adder_3_gg), .P3(n4_bit_adder_3_pg), .G2(n4_bit_adder_2_gg),
    .P2(n4_bit_adder_2_pg), .G1(n4_bit_adder_1_gg), .P1(n4_bit_adder_1_pg));  // open: C4
  // Probe on S
endmodule

module _32_bit_SignalCLA (
  input  C0,
  input  [31:0] A,
  input  [31:0] B,
  output ZF,
  output CF,
  output [31:0] out_6,
  output OF,
  output SF
);

  wire _0_15_c4, _16_31_c4, _16_31_cn_1;

  // Probe on A
  // Probe on B
  _16_bit_CLA _0_15 (.C0(C0), .A(A[15:0]), .B(B[15:0]), .C4(_0_15_c4), .S(out_6[15:0]));  // open: Cn_1, Fn_1
  _16_bit_CLA _16_31 (
    .C0(_0_15_c4), .A(A[31:16]), .B(B[31:16]), .C4(_16_31_c4), .Cn_1(_16_31_cn_1), .S(out_6[31:16]), .Fn_1(SF));
  xor xor_1 (CF, C0, _16_31_c4);
  xor xor_2 (OF, _16_31_c4, _16_31_cn_1);
  // Probe on out_6
  and and_1 (ZF, out_6[0], out_6[1], out_6[2], out_6[3], out_6[4], out_6[5], out_6[6], out_6[7], out_6[8], out_6[9], out_6[10], out_6[11], out_6[12], out_6[13], out_6[14], out_6[15], out_6[16], out_6[17], out_6[18], out_6[19], out_6[20], out_6[21], out_6[22], out_6[23], out_6[24], out_6[25], out_6[26], out_6[27], out_6[28], out_6[29], out_6[30], out_6[31]);
endmodule

module ALUCtr (
  input  [3:0] Cin,
  output SUBctr,
  output SIGctr,
  output [1:0] OPctr
);

  wire and_1_out, not_2_out, not_3_out;

  or or_1 (SUBctr, Cin[1], Cin[3]);
  not not_1 (SIGctr, Cin[0]);
  not not_2 (not_2_out, Cin[2]);
  and and_1 (and_1_out, not_2_out, Cin[1]);
  not not_3 (not_3_out, Cin[3]);
  and and_2 (OPctr[0], not_3_out, Cin[1]);
  or or_2 (OPctr[1], Cin[0], and_1_out);
endmodule

module testr (
  input  [7:0] in_1,
  output [15:0] out_2
);

  assign out_2 = {{8{1'b0}}, in_1};  // Bit_Extender bit_extender_1
endmodule

module ALU (
  input  [3:0] ALUctr,
  input  [31:0] A,
  input  [31:0] B,
  output Zero,
  output [31:0] Result
);

  wire aluctr_1_sigctr, aluctr_1_subctr, multiplexer_2_out, n32_bit_signalcla_1_cf, n32_bit_signalcla_1_of,
       n32_bit_signalcla_1_sf, xor_1_out, xor_2_out;
  wire [1:0] aluctr_1_opctr;
  wire [31:0] bit_extender_1_out, bit_extender_2_out, n32_bit_signalcla_1_out_6, orgatearray_1_out_3,
       xorgatearray_1_out_3;

  // Probe on A
  // Probe on B
  assign bit_extender_1_out = {{31{aluctr_1_subctr}}, aluctr_1_subctr};  // Bit_Extender bit_extender_1
  OrGateArray orgatearray_1 (.in_1(A), .in_2(B), .out_3(orgatearray_1_out_3));
  XORGateArray xorgatearray_1 (.in_1(B), .in_2(bit_extender_1_out), .out_3(xorgatearray_1_out_3));
  _32_bit_SignalCLA u_32_bit_signalcla_1 (
    .C0(aluctr_1_subctr), .A(A), .B(xorgatearray_1_out_3), .ZF(Zero), .CF(n32_bit_signalcla_1_cf),
    .out_6(n32_bit_signalcla_1_out_6), .OF(n32_bit_signalcla_1_of), .SF(n32_bit_signalcla_1_sf));
  xor xor_1 (xor_1_out, aluctr_1_subctr, n32_bit_signalcla_1_cf);
  xor xor_2 (xor_2_out, n32_bit_signalcla_1_of, n32_bit_signalcla_1_sf);
  Multiplexer #(.select(2), .width(32), .enable("false")) multiplexer_1 (
    .in0(n32_bit_signalcla_1_out_6), .in1(orgatearray_1_out_3), .in2(B), .in3(bit_extender_2_out),
    .out(Result), .sel(aluctr_1_opctr));
  ALUCtr aluctr_1 (.Cin(ALUctr), .SUBctr(aluctr_1_subctr), .SIGctr(aluctr_1_sigctr), .OPctr(aluctr_1_opctr));
  Multiplexer #(.enable("false")) multiplexer_2 (
    .in0(xor_1_out), .in1(xor_2_out), .out(multiplexer_2_out), .sel(aluctr_1_sigctr));
  assign bit_extender_2_out = {{31{1'b0}}, multiplexer_2_out};  // Bit_Extender bit_extender_2
  // Probe on Result
endmodule

module OrGateArray (
  input  [31:0] in_1,
  input  [31:0] in_2,
  output [31:0] out_3
);

  or or_1 (out_3[0], in_1[0], in_2[0]);
  or or_2 (out_3[1], in_1[1], in_2[1]);
  or or_3 (out_3[2], in_1[2], in_2[2]);
  or or_4 (out_3[3], in_1[3], in_2[3]);
  or or_5 (out_3[4], in_1[4], in_2[4]);
  or or_6 (out_3[5], in_1[5], in_2[5]);
  or or_7 (out_3[6], in_1[6], in_2[6]);
  or or_8 (out_3[7], in_1[7], in_2[7]);
  or or_9 (out_3[8], in_1[8], in_2[8]);
  or or_10 (out_3[9], in_1[9], in_2[9]);
  or or_11 (out_3[10], in_1[10], in_2[10]);
  or or_12 (out_3[11], in_1[11], in_2[11]);
  or or_13 (out_3[12], in_1[12], in_2[12]);
  or or_14 (out_3[13], in_1[13], in_2[13]);
  or or_15 (out_3[14], in_1[14], in_2[14]);
  or or_16 (out_3[15], in_1[15], in_2[15]);
  or or_17 (out_3[16], in_1[16], in_2[16]);
  or or_18 (out_3[17], in_1[17], in_2[17]);
  or or_19 (out_3[18], in_1[18], in_2[18]);
  or or_20 (out_3[19], in_1[19], in_2[19]);
  or or_21 (out_3[20], in_1[20], in_2[20]);
  or or_22 (out_3[21], in_1[21], in_2[21]);
  or or_23 (out_3[22], in_1[22], in_2[22]);
  or or_24 (out_3[23], in_1[23], in_2[23]);
  or or_25 (out_3[24], in_1[24], in_2[24]);
  or or_26 (out_3[25], in_1[25], in_2[25]);
  or or_27 (out_3[26], in_1[26], in_2[26]);
  or or_28 (out_3[27], in_1[27], in_2[27]);
  or or_29 (out_3[28], in_1[28], in_2[28]);
  or or_30 (out_3[29], in_1[29], in_2[29]);
  or or_31 (out_3[30], in_1[30], in_2[30]);
  or or_32 (out_3[31], in_1[31], in_2[31]);
endmodule

module XORGateArray (
  input  [31:0] in_1,
  input  [31:0] in_2,
  output [31:0] out_3
);

  xor xor_1 (out_3[0], in_1[0], in_2[0]);
  xor xor_2 (out_3[1], in_1[1], in_2[1]);
  xor xor_3 (out_3[2], in_1[2], in_2[2]);
  xor xor_4 (out_3[3], in_1[3], in_2[3]);
  xor xor_5 (out_3[4], in_1[4], in_2[4]);
  xor xor_6 (out_3[5], in_1[5], in_2[5]);
  xor xor_7 (out_3[6], in_1[6], in_2[6]);
  xor xor_8 (out_3[7], in_1[7], in_2[7]);
  xor xor_9 (out_3[8], in_1[8], in_2[8]);
  xor xor_10 (out_3[9], in_1[9], in_2[9]);
  xor xor_11 (out_3[10], in_1[10], in_2[10]);
  xor xor_12 (out_3[11], in_1[11], in_2[11]);
  xor xor_13 (out_3[12], in_1[12], in_2[12]);
  xor xor_14 (out_3[13], in_1[13], in_2[13]);
  xor xor_15 (out_3[14], in_1[14], in_2[14]);
  xor xor_16 (out_3[15], in_1[15], in_2[15]);
  xor xor_17 (out_3[16], in_1[16], in_2[16]);
  xor xor_18 (out_3[17], in_1[17], in_2[17]);
  xor xor_19 (out_3[18], in_1[18], in_2[18]);
  xor xor_20 (out_3[19], in_1[19], in_2[19]);
  xor xor_21 (out_3[20], in_1[20], in_2[20]);
  xor xor_22 (out_3[21], in_1[21], in_2[21]);
  xor xor_23 (out_3[22], in_1[22], in_2[22]);
  xor xor_24 (out_3[23], in_1[23], in_2[23]);
  xor xor_25 (out_3[24], in_1[24], in_2[24]);
  xor xor_26 (out_3[25], in_1[25], in_2[25]);
  xor xor_27 (out_3[26], in_1[26], in_2[26]);
  xor xor_28 (out_3[27], in_1[27], in_2[27]);
  xor xor_29 (out_3[28], in_1[28], in_2[28]);
  xor xor_30 (out_3[29], in_1[29], in_2[29]);
  xor xor_31 (out_3[30], in_1[30], in_2[30]);
  xor xor_32 (out_3[31], in_1[31], in_2[31]);
endmodule
