// Logisim project IFU.circ as structural Verilog: 6 circuits, main circuit main
module main (
);

  IFU ifu_1 ();  // open: imm, Branch, Zero, Jump, Instr, PC
endmodule

module IFU (
  input  [31:0] imm,
  input  Branch,
  input  Zero,
  input  Jump,
  output [31:0] Instr,
  output [31:0] PC
);

  wire and_1_out, Clk, or_1_out, Reset;
  wire [31:0] adder_1_out, multiplexer_1_out;

  and and_1 (and_1_out, Branch, Zero);
  or or_1 (or_1_out, and_1_out, Jump);
  Register #(.width(32), .trigger("falling"), .Select("low")) u_PC (
    .D(adder_1_out), .Q(PC), .clk(Clk), .clr(Reset));  // open: en
  Multiplexer #(.width(32), .enable("false")) multiplexer_1 (
    .in0(32'h4), .in1(imm), .out(multiplexer_1_out), .sel(or_1_out));
  Clock clock_1 (.out(Clk));
  Button button_1 (.out(Reset));
  Adder #(.width(32)) adder_1 (.a(PC), .b(multiplexer_1_out), .out(adder_1_out));  // open: cin, cout
  ROM #(.addrWidth(24), .dataWidth(32), .Select("low")) rom_1 (.addr(PC[23:0]), .data(Instr));
endmodule

module Main_Contral (
  input  [31:0] Instr,
  output [6:0] op,
  output [4:0] Rd,
  output [2:0] funct3,
  output [4:0] Rs1,
  output [4:0] Rs2,
  output [6:0] funct7
);

  wire [2:0] ExtOp;
  wire [31:0] imm;

  InstrTolmm instrtolmm_1 (.Instr(Instr), .out_3(imm), .ExtOp(ExtOp));

  assign funct3 = Instr[14:12];
  assign funct7 = Instr[31:25];
  assign op = Instr[6:0];
  assign Rd = Instr[11:7];
  assign Rs1 = Instr[19:15];
  assign Rs2 = Instr[24:20];
endmodule

module EXT20 (
  input  in_1,
  output [19:0] out_2
);


  assign out_2 = {20{in_1}};
endmodule

module EXT12 (
  input  in_1,
  output [11:0] out_2
);


  assign out_2 = {12{in_1}};
endmodule

module InstrTolmm (
  input  [31:0] Instr,
  input  [2:0] ExtOp,
  output [31:0] out_3
);

  wire [11:0] ext12_1_out_2;
  wire [19:0] ext20_1_out_2, ext20_2_out_2, ext20_3_out_2;

  EXT20 ext20_1 (.in_1(Instr[31]), .out_2(ext20_1_out_2));
  EXT20 ext20_2 (.in_1(Instr[31]), .out_2(ext20_2_out_2));
  EXT20 ext20_3 (.in_1(Instr[31]), .out_2(ext20_3_out_2));
  EXT12 ext12_1 (.in_1(Instr[31]), .out_2(ext12_1_out_2));
  Multiplexer #(.select(3), .width(32), .enable("false")) multiplexer_1 (
    .in0({ext20_1_out_2, Instr[31:20]}), .in1({Instr[31:12], {12{1'b0}}}),
    .in2({ext20_2_out_2, Instr[31:25], Instr[11:7]}),
    .in3({ext20_3_out_2, Instr[7], Instr[30:25], Instr[11:8], 1'b0}),
    .in4({ext12_1_out_2, Instr[19:12], Instr[20], Instr[30:21], 1'b0}), .in5({32{1'b0}}), .in6({32{1'b0}}),
    .in7({32{1'b0}}), .out(out_3), .sel(ExtOp));

  // Notes on the sheet:
  //   I型
  //   U型
  //   S型
  //   B型
  //   B型
endmodule
