// Logisim project Lab5.circ as structural Verilog
module main (
  output [31:0] Instr,
  output [6:0] funct7,
  output [31:0] Imm
);

  wire ALU_zero, and_1_out, button_1_out, Clk_out, control_1_aluasrs, control_1_branch, control_1_jump,
       control_1_memtoreg, control_1_memwr, control_1_regwr, or_1_out;
  wire [1:0] control_1_alubsrc;
  wire [2:0] control_1_extop, \指令分解_1_out_6 ;
  wire [3:0] control_1_aluctr;
  wire [4:0] \指令分解_1_out_5 , \指令分解_1_out_7 , \指令分解_1_out_8 ;
  wire [6:0] \指令分解_1_out_4 ;
  wire [31:0] ALU_result, multiplexer_1_out, multiplexer_2_out, multiplexer_3_out, n3_1_p2, n3_1_p7, n3_1_p8,
       n32_bit_signalcla_1_out_6, \n32_bit数据存储器_1_d , PC_q;

  Clock Clk (.out(Clk_out));
  Button button_1 (.out(button_1_out));
  Register #(.width(32), .Select("low")) PC (
    .D(n32_bit_signalcla_1_out_6), .Q(PC_q), .clk(Clk_out), .clr(button_1_out));  // open: en
  Multiplexer #(.width(32), .enable("false")) multiplexer_1 (
    .in0(32'h4), .in1(Imm), .out(multiplexer_1_out), .sel(or_1_out));
  or or_1 (or_1_out, control_1_jump, and_1_out);
  and and_1 (and_1_out, control_1_branch, ALU_zero);
  Multiplexer #(.select(2), .width(32), .enable("false")) multiplexer_2 (
    .in0(n3_1_p8), .in1(32'h4), .in2(Imm), .in3({32{1'b0}}), .out(multiplexer_2_out), .sel(control_1_alubsrc));
  _32_bit_SignalCLA u_32_bit_signalcla_1 (
    .C0(1'b0), .A(PC_q), .B(multiplexer_1_out), .out_6(n32_bit_signalcla_1_out_6));  // open: ZF, CF, OF, SF
  Multiplexer #(.width(32), .enable("false")) multiplexer_3 (
    .in0(n3_1_p7), .in1(PC_q), .out(multiplexer_3_out), .sel(control_1_aluasrs));
  ALU ALU (
    .Zero(ALU_zero), .Result(ALU_result), .A(multiplexer_3_out), .B(multiplexer_2_out),
    .ALUctr(control_1_aluctr));
  RAM #(.addrWidth(12), .dataWidth(32), .Select("low")) ram_1 (
    .addr(PC_q[13:2]), .data(Instr), .clk(Clk_out), .clr(button_1_out));  // open: sel, ld
  \指令分解  \u_指令分解_1  (
    .\输入指令 (Instr), .ExtOp(control_1_extop), .out_4(\指令分解_1_out_4 ), .out_5(\指令分解_1_out_5 ),
    .out_6(\指令分解_1_out_6 ), .out_7(\指令分解_1_out_7 ), .out_8(\指令分解_1_out_8 ), .out_9(funct7), .Imm(Imm));
  Control control_1 (
    .funct3(\指令分解_1_out_6 ), .op(\指令分解_1_out_4 ), .Branch(control_1_branch), .Jump(control_1_jump),
    .ALUASrs(control_1_aluasrs), .ALUBSrc(control_1_alubsrc), .ALUctr(control_1_aluctr),
    .MemtoReg(control_1_memtoreg), .RegWr(control_1_regwr), .MemWr(control_1_memwr), .ExtOp(control_1_extop));
  // _3 3_1: pin names not known; wires that end beside it: \指令分解_1_out_5 , n3_1_p2, \指令分解_1_out_7 , Clk_out, \指令分解_1_out_8 , control_1_regwr, n3_1_p7, n3_1_p8
  Multiplexer #(.width(32), .enable("false")) multiplexer_4 (
    .in0(ALU_result), .in1(\n32_bit数据存储器_1_d ), .out(n3_1_p2), .sel(control_1_memtoreg));
  \_32_bit数据存储器  \u_32_bit数据存储器_1  (
    .Address(ALU_result), .Data_In(n3_1_p8), .Clk(Clk_out), .WriteEnable(control_1_memwr),
    .D(\n32_bit数据存储器_1_d ));
endmodule

module RAM_Test (
  input  [11:0] in_1,
  input  [31:0] in_2,
  input  \输入使能 ,
  input  \片选 ,
  input  \输出使能 ,
  output [31:0] out_6
);

  wire \复位按钮_out , \时钟信号_out ;
  wire [6:0] undriven;

  Clock \u_时钟信号  (.out(\时钟信号_out ));
  Button \u_复位按钮  (.out(\复位按钮_out ));
  RAM #(.addrWidth(12), .dataWidth(32), .bus("separate"), .Select("low")) ram_1 (
    .addr(in_1), .din(in_2), .data(out_6), .str(\输入使能 ), .sel(\片选 ), .clk(\时钟信号_out ), .ld(\输出使能 ),
    .clr(\复位按钮_out ));
  TTY tty_1 (.data(undriven), .clk(\时钟信号_out ), .clr(\复位按钮_out ));  // open: we
endmodule

module _2 (
  input  [31:0] Imm,
  input  Jump,
  input  [2:0] in_3,
  input  Branch,
  input  Zero,
  output [31:0] Instr,
  output [6:0] op,
  output [4:0] Rd,
  output [2:0] funct3,
  output [4:0] Rs1,
  output [4:0] Rs2,
  output [6:0] funct7,
  output [31:0] Imm_2
);

  wire and_1_out, button_1_out, Clk_out, or_1_out;
  wire [31:0] multiplexer_1_out, n32_bit_signalcla_1_out_6, PC_q;

  Clock Clk (.out(Clk_out));
  Button button_1 (.out(button_1_out));
  Register #(.width(32), .Select("low")) PC (
    .D(n32_bit_signalcla_1_out_6), .Q(PC_q), .clk(Clk_out), .clr(button_1_out));  // open: en
  Multiplexer #(.width(32), .enable("false")) multiplexer_1 (
    .in0(32'h4), .in1(Imm), .out(multiplexer_1_out), .sel(or_1_out));
  or or_1 (or_1_out, Jump, and_1_out);
  and and_1 (and_1_out, Branch, Zero);
  _32_bit_SignalCLA u_32_bit_signalcla_1 (
    .C0(1'b0), .A(PC_q), .B(multiplexer_1_out), .out_6(n32_bit_signalcla_1_out_6));  // open: ZF, CF, OF, SF
  ROM #(.addrWidth(12), .dataWidth(32), .Select("low")) \u_指令存储器  (.addr(PC_q[13:2]), .data(Instr));
  \指令分解  \u_指令分解_1  (
    .\输入指令 (Instr), .ExtOp(in_3), .out_4(op), .out_5(Rd), .out_6(funct3), .out_7(Rs1), .out_8(Rs2),
    .out_9(funct7), .Imm(Imm_2));

  // Notes on the sheet:
  //   contents of 指令存储器 (hex, n*v repeats v):
  //   102*0 10010 10110111 11111111 11110010 10000010 10010011 101 11011110 11000 1100011 101000 10000000
  //   0 11101111 0 10001 100110 100011
endmodule

module \指令分解  (
  input  [31:0] \输入指令 ,
  input  [2:0] ExtOp,
  output [31:0] Imm,
  output [6:0] out_4,
  output [4:0] out_5,
  output [2:0] out_6,
  output [4:0] out_7,
  output [4:0] out_8,
  output [6:0] out_9
);

  InstrTolmm instrtolmm_1 (.Instr(\输入指令 ), .Extop(ExtOp), .imm(Imm));

  assign out_4 = \输入指令 [6:0];
  assign out_5 = \输入指令 [11:7];
  assign out_6 = \输入指令 [14:12];
  assign out_7 = \输入指令 [19:15];
  assign out_8 = \输入指令 [24:20];
  assign out_9 = \输入指令 [31:25];

  // Other names for the same wires on the sheet: op[6:0] = \输入指令 [6:0]; Rd[4:0] = \输入指令 [11:7];
  //   funct3[2:0] = \输入指令 [14:12]; Rs1[4:0] = \输入指令 [19:15]; Rs2[4:0] = \输入指令 [24:20]; funct7[6:0] = \输入指令 [31:25]
endmodule

module InstrTolmm (
  input  [31:0] Instr,
  input  [2:0] Extop,
  output [31:0] imm
);

  wire [11:0] bit_extender_4_out;
  wire [19:0] bit_extender_1_out, bit_extender_2_out, bit_extender_3_out;

  assign bit_extender_1_out = {{19{Instr[31]}}, Instr[31]};  // Bit_Extender bit_extender_1
  assign bit_extender_2_out = {{19{Instr[31]}}, Instr[31]};  // Bit_Extender bit_extender_2
  assign bit_extender_3_out = {{19{Instr[31]}}, Instr[31]};  // Bit_Extender bit_extender_3
  assign bit_extender_4_out = {{11{Instr[31]}}, Instr[31]};  // Bit_Extender bit_extender_4
  Multiplexer #(.select(3), .width(32), .enable("false")) multiplexer_1 (
    .in0({bit_extender_1_out, Instr[31:20]}), .in1({Instr[31:12], {12{1'b0}}}),
    .in2({bit_extender_2_out, Instr[31:25], Instr[11:7]}),
    .in3({bit_extender_3_out, Instr[7], Instr[30:25], Instr[11:8], 1'b0}),
    .in4({bit_extender_4_out, Instr[19:12], Instr[31:21], 1'b0}), .in5({32{1'b0}}), .in6({32{1'b0}}),
    .in7({32{1'b0}}), .out(imm), .sel(Extop));

  // Notes on the sheet:
  //   I
  //   U
  //   S
  //   B
  //   J
endmodule

module _32_32_bit_Registers (
  input  [4:0] Rs1,
  input  [4:0] Rs2,
  input  [4:0] RW,
  input  [31:0] busW,
  input  WE,
  input  CLK,
  output [31:0] busA,
  output [31:0] busB
);

  wire and_1_out, and_2_out, and_3_out, and_4_out, and_5_out, and_6_out, and_7_out, and_8_out, and_9_out,
       and_10_out, and_11_out, and_12_out, and_13_out, and_14_out, and_15_out, and_16_out, and_17_out,
       and_18_out, and_19_out, and_20_out, and_21_out, and_22_out, and_23_out, and_24_out, and_25_out,
       and_26_out, and_27_out, and_28_out, and_29_out, and_30_out, and_31_out, and_32_out, decoder_1_out0,
       decoder_1_out1, decoder_1_out2, decoder_1_out3, decoder_1_out4, decoder_1_out5, decoder_1_out6,
       decoder_1_out7, decoder_1_out8, decoder_1_out9, decoder_1_out10, decoder_1_out11, decoder_1_out12,
       decoder_1_out13, decoder_1_out14, decoder_1_out15, decoder_1_out16, decoder_1_out17, decoder_1_out18,
       decoder_1_out19, decoder_1_out20, decoder_1_out21, decoder_1_out22, decoder_1_out23, decoder_1_out24,
       decoder_1_out25, decoder_1_out26, decoder_1_out27, decoder_1_out28, decoder_1_out29, decoder_1_out30,
       decoder_1_out31;
  wire [31:0] register_1_q, register_2_q, register_3_q, register_4_q, register_5_q, register_6_q,
       register_7_q, register_8_q, register_9_q, register_10_q, register_11_q, register_12_q, register_13_q,
       register_14_q, register_15_q, register_16_q, register_17_q, register_18_q, register_19_q,
       register_20_q, register_21_q, register_22_q, register_23_q, register_24_q, register_25_q,
       register_26_q, register_27_q, register_28_q, register_29_q, register_30_q, register_31_q,
       register_32_q;

  Decoder #(.select(5), .enable("false")) decoder_1 (
    .out0(decoder_1_out0), .out1(decoder_1_out1), .out2(decoder_1_out2), .out3(decoder_1_out3),
    .out4(decoder_1_out4), .out5(decoder_1_out5), .out6(decoder_1_out6), .out7(decoder_1_out7),
    .out8(decoder_1_out8), .out9(decoder_1_out9), .out10(decoder_1_out10), .out11(decoder_1_out11),
    .out12(decoder_1_out12), .out13(decoder_1_out13), .out14(decoder_1_out14), .out15(decoder_1_out15),
    .out16(decoder_1_out16), .out17(decoder_1_out17), .out18(decoder_1_out18), .out19(decoder_1_out19),
    .out20(decoder_1_out20), .out21(decoder_1_out21), .out22(decoder_1_out22), .out23(decoder_1_out23),
    .out24(decoder_1_out24), .out25(decoder_1_out25), .out26(decoder_1_out26), .out27(decoder_1_out27),
    .out28(decoder_1_out28), .out29(decoder_1_out29), .out30(decoder_1_out30), .out31(decoder_1_out31),
    .sel(RW));
  and and_1 (and_1_out, CLK, WE, decoder_1_out0);
  and and_2 (and_2_out, CLK, WE, decoder_1_out1);
  and and_3 (and_3_out, CLK, WE, decoder_1_out2);
  and and_4 (and_4_out, CLK, WE, decoder_1_out3);
  and and_5 (and_5_out, CLK, WE, decoder_1_out4);
  and and_6 (and_6_out, CLK, WE, decoder_1_out5);
  and and_7 (and_7_out, CLK, WE, decoder_1_out6);
  and and_8 (and_8_out, CLK, WE, decoder_1_out7);
  and and_9 (and_9_out, CLK, WE, decoder_1_out8);
  and and_10 (and_10_out, CLK, WE, decoder_1_out9);
  and and_11 (and_11_out, CLK, WE, decoder_1_out10);
  and and_12 (and_12_out, CLK, WE, decoder_1_out11);
  and and_13 (and_13_out, CLK, WE, decoder_1_out12);
  and and_14 (and_14_out, CLK, WE, decoder_1_out13);
  and and_15 (and_15_out, CLK, WE, decoder_1_out14);
  and and_16 (and_16_out, CLK, WE, decoder_1_out15);
  and and_17 (and_17_out, CLK, WE, decoder_1_out16);
  and and_18 (and_18_out, CLK, WE, decoder_1_out17);
  and and_19 (and_19_out, CLK, WE, decoder_1_out18);
  and and_20 (and_20_out, CLK, WE, decoder_1_out19);
  and and_21 (and_21_out, CLK, WE, decoder_1_out20);
  and and_22 (and_22_out, CLK, WE, decoder_1_out21);
  and and_23 (and_23_out, CLK, WE, decoder_1_out22);
  and and_24 (and_24_out, CLK, WE, decoder_1_out23);
  and and_25 (and_25_out, CLK, WE, decoder_1_out24);
  and and_26 (and_26_out, CLK, WE, decoder_1_out25);
  and and_27 (and_27_out, CLK, WE, decoder_1_out26);
  and and_28 (and_28_out, CLK, WE, decoder_1_out27);
  and and_29 (and_29_out, CLK, WE, decoder_1_out28);
  and and_30 (and_30_out, CLK, WE, decoder_1_out29);
  and and_31 (and_31_out, CLK, WE, decoder_1_out30);
  and and_32 (and_32_out, CLK, WE, decoder_1_out31);
  Register #(.width(32), .Select("low")) register_1 (.D(busW), .Q(register_1_q), .clk(and_1_out));  // open: en, clr
  Register #(.width(32), .Select("low")) register_2 (.D(busW), .Q(register_2_q), .clk(and_2_out));  // open: en, clr
  Register #(.width(32), .Select("low")) register_3 (.D(busW), .Q(register_3_q), .clk(and_3_out));  // open: en, clr
  Register #(.width(32), .Select("low")) register_4 (.D(busW), .Q(register_4_q), .clk(and_4_out));  // open: en, clr
  Register #(.width(32), .Select("low")) register_5 (.D(busW), .Q(register_5_q), .clk(and_5_out));  // open: en, clr
  Register #(.width(32), .Select("low")) register_6 (.D(busW), .Q(register_6_q), .clk(and_6_out));  // open: en, clr
  Register #(.width(32), .Select("low")) register_7 (.D(busW), .Q(register_7_q), .clk(and_7_out));  // open: en, clr
  Register #(.width(32), .Select("low")) register_8 (.D(busW), .Q(register_8_q), .clk(and_8_out));  // open: en, clr
  Register #(.width(32), .Select("low")) register_9 (.D(busW), .Q(register_9_q), .clk(and_9_out));  // open: en, clr
  Register #(.width(32), .Select("low")) register_10 (.D(busW), .Q(register_10_q), .clk(and_10_out));  // open: en, clr
  Register #(.width(32), .Select("low")) register_11 (.D(busW), .Q(register_11_q), .clk(and_11_out));  // open: en, clr
  Register #(.width(32), .Select("low")) register_12 (.D(busW), .Q(register_12_q), .clk(and_12_out));  // open: en, clr
  Register #(.width(32), .Select("low")) register_13 (.D(busW), .Q(register_13_q), .clk(and_13_out));  // open: en, clr
  Register #(.width(32), .Select("low")) register_14 (.D(busW), .Q(register_14_q), .clk(and_14_out));  // open: en, clr
  Register #(.width(32), .Select("low")) register_15 (.D(busW), .Q(register_15_q), .clk(and_15_out));  // open: en, clr
  Register #(.width(32), .Select("low")) register_16 (.D(busW), .Q(register_16_q), .clk(and_16_out));  // open: en, clr
  Register #(.width(32), .Select("low")) register_17 (.D(busW), .Q(register_17_q), .clk(and_17_out));  // open: en, clr
  Register #(.width(32), .Select("low")) register_18 (.D(busW), .Q(register_18_q), .clk(and_18_out));  // open: en, clr
  Register #(.width(32), .Select("low")) register_19 (.D(busW), .Q(register_19_q), .clk(and_19_out));  // open: en, clr
  Register #(.width(32), .Select("low")) register_20 (.D(busW), .Q(register_20_q), .clk(and_20_out));  // open: en, clr
  Register #(.width(32), .Select("low")) register_21 (.D(busW), .Q(register_21_q), .clk(and_21_out));  // open: en, clr
  Register #(.width(32), .Select("low")) register_22 (.D(busW), .Q(register_22_q), .clk(and_22_out));  // open: en, clr
  Register #(.width(32), .Select("low")) register_23 (.D(busW), .Q(register_23_q), .clk(and_23_out));  // open: en, clr
  Register #(.width(32), .Select("low")) register_24 (.D(busW), .Q(register_24_q), .clk(and_24_out));  // open: en, clr
  Register #(.width(32), .Select("low")) register_25 (.D(busW), .Q(register_25_q), .clk(and_25_out));  // open: en, clr
  Register #(.width(32), .Select("low")) register_26 (.D(busW), .Q(register_26_q), .clk(and_26_out));  // open: en, clr
  Register #(.width(32), .Select("low")) register_27 (.D(busW), .Q(register_27_q), .clk(and_27_out));  // open: en, clr
  Register #(.width(32), .Select("low")) register_28 (.D(busW), .Q(register_28_q), .clk(and_28_out));  // open: en, clr
  Register #(.width(32), .Select("low")) register_29 (.D(busW), .Q(register_29_q), .clk(and_29_out));  // open: en, clr
  Register #(.width(32), .Select("low")) register_30 (.D(busW), .Q(register_30_q), .clk(and_30_out));  // open: en, clr
  Register #(.width(32), .Select("low")) register_31 (.D(busW), .Q(register_31_q), .clk(and_31_out));  // open: en, clr
  Register #(.width(32), .Select("low")) register_32 (.D(busW), .Q(register_32_q), .clk(and_32_out));  // open: en, clr
  Multiplexer #(.select(5), .width(32), .enable("false")) multiplexer_1 (
    .in0(register_1_q), .in1(register_2_q), .in2(register_3_q), .in3(register_4_q), .in4(register_5_q),
    .in5(register_6_q), .in6(register_7_q), .in7(register_8_q), .in8(register_9_q), .in9(register_10_q),
    .in10(register_11_q), .in11(register_12_q), .in12(register_13_q), .in13(register_14_q),
    .in14(register_15_q), .in15(register_16_q), .in16(register_17_q), .in17(register_18_q),
    .in18(register_19_q), .in19(register_20_q), .in20(register_21_q), .in21(register_22_q),
    .in22(register_23_q), .in23(register_24_q), .in24(register_25_q), .in25(register_26_q),
    .in26(register_27_q), .in27(register_28_q), .in28(register_29_q), .in29(register_30_q),
    .in30(register_31_q), .in31(register_32_q));  // open: out, sel
  Multiplexer #(.select(5), .width(32), .enable("false")) multiplexer_2 (
    .in0(register_1_q), .in1(register_2_q), .in2(register_3_q), .in3(register_4_q), .in4(register_5_q),
    .in5(register_6_q), .in6(register_7_q), .in7(register_8_q), .in8(register_9_q), .in9(register_10_q),
    .in10(register_11_q), .in11(register_12_q), .in12(register_13_q), .in13(register_14_q),
    .in14(register_15_q), .in15(register_16_q), .in16(register_17_q), .in17(register_18_q),
    .in18(register_19_q), .in19(register_20_q), .in20(register_21_q), .in21(register_22_q),
    .in22(register_23_q), .in23(register_24_q), .in24(register_25_q), .in25(register_26_q),
    .in26(register_27_q), .in27(register_28_q), .in28(register_29_q), .in29(register_30_q),
    .in30(register_31_q), .in31(register_32_q), .out(busA), .sel(Rs1));
  Multiplexer #(.select(5), .width(32), .enable("false")) multiplexer_3 (
    .in0(register_1_q), .in1(register_2_q), .in2(register_3_q), .in3(register_4_q), .in4(register_5_q),
    .in5(register_6_q), .in6(register_7_q), .in7(register_8_q), .in8(register_9_q), .in9(register_10_q),
    .in10(register_11_q), .in11(register_12_q), .in12(register_13_q), .in13(register_14_q),
    .in14(register_15_q), .in15(register_16_q), .in16(register_17_q), .in17(register_18_q),
    .in18(register_19_q), .in19(register_20_q), .in20(register_21_q), .in21(register_22_q),
    .in22(register_23_q), .in23(register_24_q), .in24(register_25_q), .in25(register_26_q),
    .in26(register_27_q), .in27(register_28_q), .in28(register_29_q), .in29(register_30_q),
    .in30(register_31_q), .in31(register_32_q), .out(busB), .sel(Rs2));
endmodule

module \_25_bit数据存储器  (
  input  [24:0] Address,
  input  [31:0] Data_In,
  input  Clk,
  input  WrEn,
  output [31:0] D
);

  wire [23:0] demultiplexer_1_out0, demultiplexer_1_out1;
  wire [31:0] ram_1_data, ram_2_data;

  Demultiplexer #(.width(24), .enable("false")) demultiplexer_1 (
    .out0(demultiplexer_1_out0), .out1(demultiplexer_1_out1), .in(Address[23:0]), .sel(Address[24]));
  RAM #(.addrWidth(24), .dataWidth(32), .bus("separate"), .Select("low")) ram_1 (
    .addr(demultiplexer_1_out0), .din(Data_In), .data(ram_1_data), .str(1'b1), .clk(Clk), .ld(WrEn));  // open: sel, clr
  RAM #(.addrWidth(24), .dataWidth(32), .bus("separate"), .Select("low")) ram_2 (
    .addr(demultiplexer_1_out1), .din(Data_In), .data(ram_2_data), .str(1'b1), .clk(Clk), .ld(WrEn));  // open: sel, clr
  Multiplexer #(.width(32), .enable("false")) multiplexer_1 (
    .in0(ram_1_data), .in1(ram_2_data), .out(D), .sel(Address[24]));
endmodule

module \_26_bit数据存储器  (
  input  [25:0] Address,
  input  [31:0] Data_In,
  input  Clk,
  input  WriteEnable,
  output [31:0] D
);

  wire [24:0] demultiplexer_1_out0, demultiplexer_1_out1;
  wire [31:0] \n25_bit数据存储器_1_d , \n25_bit数据存储器_2_d ;

  Demultiplexer #(.width(25), .enable("false")) demultiplexer_1 (
    .out0(demultiplexer_1_out0), .out1(demultiplexer_1_out1), .in(Address[24:0]), .sel(Address[25]));
  \_25_bit数据存储器  \u_25_bit数据存储器_1  (
    .Address(demultiplexer_1_out0), .Data_In(Data_In), .Clk(Clk), .WrEn(WriteEnable), .D(\n25_bit数据存储器_1_d ));
  \_25_bit数据存储器  \u_25_bit数据存储器_2  (
    .Address(demultiplexer_1_out1), .Data_In(Data_In), .Clk(Clk), .WrEn(WriteEnable), .D(\n25_bit数据存储器_2_d ));
  Multiplexer #(.width(32), .enable("false")) multiplexer_1 (
    .in0(\n25_bit数据存储器_1_d ), .in1(\n25_bit数据存储器_2_d ), .out(D), .sel(Address[25]));
endmodule

module \_27_bit数据存储器  (
  input  [26:0] Address,
  input  [31:0] Data_In,
  input  Clk,
  input  WriteEnable,
  output [31:0] D
);

  wire [25:0] demultiplexer_1_out0, demultiplexer_1_out1;
  wire [31:0] \n26_bit数据存储器_1_d , \n26_bit数据存储器_2_d ;

  Demultiplexer #(.width(26), .enable("false")) demultiplexer_1 (
    .out0(demultiplexer_1_out0), .out1(demultiplexer_1_out1), .in(Address[25:0]), .sel(Address[26]));
  \_26_bit数据存储器  \u_26_bit数据存储器_1  (
    .Address(demultiplexer_1_out0), .Data_In(Data_In), .Clk(Clk), .WriteEnable(WriteEnable),
    .D(\n26_bit数据存储器_1_d ));
  \_26_bit数据存储器  \u_26_bit数据存储器_2  (
    .Address(demultiplexer_1_out1), .Data_In(Data_In), .Clk(Clk), .WriteEnable(WriteEnable),
    .D(\n26_bit数据存储器_2_d ));
  Multiplexer #(.width(32), .enable("false")) multiplexer_1 (
    .in0(\n26_bit数据存储器_1_d ), .in1(\n26_bit数据存储器_2_d ), .out(D), .sel(Address[26]));
endmodule

module \_28_bit数据存储器  (
  input  [27:0] Address,
  input  [31:0] Data_In,
  input  Clk,
  input  WriteEnable,
  output [31:0] D
);

  wire [26:0] demultiplexer_1_out0, demultiplexer_1_out1;
  wire [31:0] \n27_bit数据存储器_1_d , \n27_bit数据存储器_2_d ;

  Demultiplexer #(.width(27), .enable("false")) demultiplexer_1 (
    .out0(demultiplexer_1_out0), .out1(demultiplexer_1_out1), .in(Address[26:0]), .sel(Address[27]));
  \_27_bit数据存储器  \u_27_bit数据存储器_1  (
    .Address(demultiplexer_1_out0), .Data_In(Data_In), .Clk(Clk), .WriteEnable(WriteEnable),
    .D(\n27_bit数据存储器_1_d ));
  \_27_bit数据存储器  \u_27_bit数据存储器_2  (
    .Address(demultiplexer_1_out1), .Data_In(Data_In), .Clk(Clk), .WriteEnable(WriteEnable),
    .D(\n27_bit数据存储器_2_d ));
  Multiplexer #(.width(32), .enable("false")) multiplexer_1 (
    .in0(\n27_bit数据存储器_1_d ), .in1(\n27_bit数据存储器_2_d ), .out(D), .sel(Address[27]));
endmodule

module \_29_bit数据存储器  (
  input  [28:0] Address,
  input  [31:0] Data_In,
  input  Clk,
  input  WriteEnable,
  output [31:0] D
);

  wire [27:0] demultiplexer_1_out0, demultiplexer_1_out1;
  wire [31:0] \n28_bit数据存储器_1_d , \n28_bit数据存储器_2_d ;

  Demultiplexer #(.width(28), .enable("false")) demultiplexer_1 (
    .out0(demultiplexer_1_out0), .out1(demultiplexer_1_out1), .in(Address[27:0]), .sel(Address[28]));
  \_28_bit数据存储器  \u_28_bit数据存储器_1  (
    .Address(demultiplexer_1_out0), .Data_In(Data_In), .Clk(Clk), .WriteEnable(WriteEnable),
    .D(\n28_bit数据存储器_1_d ));
  \_28_bit数据存储器  \u_28_bit数据存储器_2  (
    .Address(demultiplexer_1_out1), .Data_In(Data_In), .Clk(Clk), .WriteEnable(WriteEnable),
    .D(\n28_bit数据存储器_2_d ));
  Multiplexer #(.width(32), .enable("false")) multiplexer_1 (
    .in0(\n28_bit数据存储器_1_d ), .in1(\n28_bit数据存储器_2_d ), .out(D), .sel(Address[28]));
endmodule

module \_30_bit数据存储器  (
  input  [29:0] Address,
  input  [31:0] Data_In,
  input  Clk,
  input  WriteEnable,
  output [31:0] D
);

  wire [28:0] demultiplexer_1_out0, demultiplexer_1_out1;
  wire [31:0] \n29_bit数据存储器_1_d , \n29_bit数据存储器_2_d ;

  Demultiplexer #(.width(29), .enable("false")) demultiplexer_1 (
    .out0(demultiplexer_1_out0), .out1(demultiplexer_1_out1), .in(Address[28:0]), .sel(Address[29]));
  \_29_bit数据存储器  \u_29_bit数据存储器_1  (
    .Address(demultiplexer_1_out0), .Data_In(Data_In), .Clk(Clk), .WriteEnable(WriteEnable),
    .D(\n29_bit数据存储器_1_d ));
  \_29_bit数据存储器  \u_29_bit数据存储器_2  (
    .Address(demultiplexer_1_out1), .Data_In(Data_In), .Clk(Clk), .WriteEnable(WriteEnable),
    .D(\n29_bit数据存储器_2_d ));
  Multiplexer #(.width(32), .enable("false")) multiplexer_1 (
    .in0(\n29_bit数据存储器_1_d ), .in1(\n29_bit数据存储器_2_d ), .out(D), .sel(Address[29]));
endmodule

module \_31_bit数据存储器  (
  input  [30:0] Address,
  input  [31:0] Data_In,
  input  Clk,
  input  WriteEnable,
  output [31:0] D
);

  wire [29:0] demultiplexer_1_out0, demultiplexer_1_out1;
  wire [31:0] \n30_bit数据存储器_1_d , \n30_bit数据存储器_2_d ;

  Demultiplexer #(.width(30), .enable("false")) demultiplexer_1 (
    .out0(demultiplexer_1_out0), .out1(demultiplexer_1_out1), .in(Address[29:0]), .sel(Address[30]));
  \_30_bit数据存储器  \u_30_bit数据存储器_1  (
    .Address(demultiplexer_1_out0), .Data_In(Data_In), .Clk(Clk), .WriteEnable(WriteEnable),
    .D(\n30_bit数据存储器_1_d ));
  \_30_bit数据存储器  \u_30_bit数据存储器_2  (
    .Address(demultiplexer_1_out1), .Data_In(Data_In), .Clk(Clk), .WriteEnable(WriteEnable),
    .D(\n30_bit数据存储器_2_d ));
  Multiplexer #(.width(32), .enable("false")) multiplexer_1 (
    .in0(\n30_bit数据存储器_1_d ), .in1(\n30_bit数据存储器_2_d ), .out(D), .sel(Address[30]));
endmodule

module \_32_bit数据存储器  (
  input  [31:0] Address,
  input  [31:0] Data_In,
  input  Clk,
  input  WriteEnable,
  output [31:0] D
);

  wire [30:0] demultiplexer_1_out0, demultiplexer_1_out1;
  wire [31:0] \n31_bit数据存储器_1_d , \n31_bit数据存储器_2_d ;

  Demultiplexer #(.width(31), .enable("false")) demultiplexer_1 (
    .out0(demultiplexer_1_out0), .out1(demultiplexer_1_out1), .in(Address[30:0]), .sel(Address[31]));
  \_31_bit数据存储器  \u_31_bit数据存储器_1  (
    .Address(demultiplexer_1_out0), .Data_In(Data_In), .Clk(Clk), .WriteEnable(WriteEnable),
    .D(\n31_bit数据存储器_1_d ));
  \_31_bit数据存储器  \u_31_bit数据存储器_2  (
    .Address(demultiplexer_1_out1), .Data_In(Data_In), .Clk(Clk), .WriteEnable(WriteEnable),
    .D(\n31_bit数据存储器_2_d ));
  Multiplexer #(.width(32), .enable("false")) multiplexer_1 (
    .in0(\n31_bit数据存储器_1_d ), .in1(\n31_bit数据存储器_2_d ), .out(D), .sel(Address[31]));
endmodule

module Control (
  input  [2:0] funct3,
  input  [6:0] op,
  output Branch,
  output Jump,
  output ALUASrs,
  output [1:0] ALUBSrc,
  output [3:0] ALUctr,
  output MemtoReg,
  output RegWr,
  output MemWr,
  output [2:0] ExtOp
);

  wire and_3_out, and_4_out, and_5_out, and_6_out, and_7_out, and_8_out, and_9_out, and_10_out, and_11_out,
       and_13_out, and_14_out, and_16_out, and_17_out, and_18_out, and_19_out, not_1_out, not_2_out,
       not_3_out, not_4_out, not_5_out, not_6_out, not_7_out, not_8_out, not_9_out, not_10_out, not_11_out,
       not_12_out, not_13_out, not_14_out, not_15_out, not_16_out, not_17_out, not_18_out, not_19_out,
       not_20_out, not_21_out, not_22_out, not_23_out, not_24_out, not_25_out, not_26_out, not_27_out,
       not_28_out, not_29_out, not_30_out, not_31_out, not_32_out, not_33_out, not_34_out, not_35_out,
       not_36_out, not_37_out, not_38_out, not_39_out, not_40_out, not_41_out, not_42_out, not_43_out,
       not_44_out, not_45_out, not_46_out, not_47_out, not_48_out, not_49_out, not_50_out, not_51_out,
       not_52_out, not_53_out, not_54_out, not_55_out, not_56_out, not_57_out, not_58_out, not_59_out,
       not_60_out, not_61_out, not_62_out, not_63_out, not_64_out, not_65_out;

  not not_1 (not_1_out, op[2]);
  not not_2 (not_2_out, op[4]);
  not not_3 (not_3_out, op[3]);
  and and_1 (Branch, op[6], op[6], not_2_out, not_3_out, not_1_out, op[1], op[0]);
  not not_4 (not_4_out, op[4]);
  and and_2 (ALUASrs, op[6], op[6], not_4_out, op[3], op[2], op[1], op[0]);
  not not_5 (not_5_out, op[3]);
  not not_6 (not_6_out, op[6]);
  not not_7 (not_7_out, op[6]);
  and and_3 (and_3_out, not_6_out, not_7_out, op[4], not_5_out, not_12_out);
  not not_8 (not_8_out, op[6]);
  not not_9 (not_9_out, op[3]);
  not not_10 (not_10_out, op[6]);
  not not_11 (not_11_out, op[6]);
  not not_12 (not_12_out, op[2]);
  and and_4 (and_4_out, not_8_out, op[6], op[4], not_9_out, op[2]);
  or or_1 (ALUBSrc[1], and_3_out, and_4_out, and_6_out, and_5_out);
  not not_13 (not_13_out, op[3]);
  not not_14 (not_14_out, op[4]);
  not not_15 (not_15_out, op[4]);
  not not_16 (not_16_out, op[6]);
  not not_17 (not_17_out, op[3]);
  not not_18 (not_18_out, op[2]);
  not not_19 (not_19_out, op[2]);
  and and_5 (and_5_out, not_16_out, op[6], not_15_out, not_17_out, not_18_out);
  and and_6 (and_6_out, not_11_out, not_10_out, not_14_out, not_13_out, not_19_out);
  not not_20 (not_20_out, op[6]);
  not not_21 (not_21_out, op[3]);
  and and_7 (and_7_out, not_20_out, op[6], op[4], not_21_out, op[2]);
  or or_2 (ALUctr[3], and_7_out, and_9_out);
  not not_22 (not_22_out, op[3]);
  not not_23 (not_23_out, op[4]);
  not not_24 (not_24_out, op[6]);
  not not_25 (not_25_out, op[2]);
  not not_26 (not_26_out, op[6]);
  and and_8 (and_8_out, not_24_out, not_26_out, op[4], not_27_out, not_29_out);
  and and_9 (and_9_out, op[6], op[6], not_23_out, not_22_out, not_25_out);
  or or_3 (ALUctr[2], and_7_out, and_8_out);
  not not_27 (not_27_out, op[3]);
  not not_28 (not_28_out, op[3]);
  not not_29 (not_29_out, op[2]);
  not not_30 (not_30_out, op[6]);
  and and_10 (and_10_out, not_30_out, op[6], op[4], not_28_out, not_32_out, not_35_out, funct3[1], not_34_out);
  or or_4 (ALUctr[1], and_7_out, and_8_out, and_10_out, and_11_out);
  not not_31 (not_31_out, op[3]);
  not not_32 (not_32_out, op[2]);
  not not_33 (not_33_out, op[6]);
  not not_34 (not_34_out, funct3[0]);
  not not_35 (not_35_out, funct3[2]);
  or or_5 (ALUctr[0], and_7_out, and_11_out);
  not not_36 (not_36_out, op[2]);
  not not_37 (not_37_out, funct3[2]);
  and and_11 (and_11_out, not_33_out, op[6], op[4], not_31_out, not_36_out, not_37_out, funct3[1], funct3[0]);
  not not_38 (not_38_out, op[6]);
  not not_39 (not_39_out, op[6]);
  not not_40 (not_40_out, op[4]);
  and and_12 (MemtoReg, not_39_out, not_38_out, not_40_out, not_45_out, not_46_out);
  not not_41 (not_41_out, op[2]);
  not not_42 (not_42_out, op[4]);
  not not_43 (not_43_out, op[3]);
  not not_44 (not_44_out, op[6]);
  and and_13 (and_13_out, not_44_out, op[6], not_42_out, not_43_out, not_41_out);
  not not_45 (not_45_out, op[3]);
  not not_46 (not_46_out, op[2]);
  nor nor_1 (RegWr, and_13_out, and_14_out);
  not not_47 (not_47_out, op[3]);
  not not_48 (not_48_out, op[2]);
  not not_49 (not_49_out, op[4]);
  and and_14 (and_14_out, op[6], op[6], not_49_out, not_47_out, not_48_out);
  not not_50 (not_50_out, op[3]);
  not not_51 (not_51_out, op[6]);
  not not_52 (not_52_out, op[4]);
  and and_15 (MemWr, not_51_out, op[6], not_52_out, not_50_out, not_57_out);
  not not_53 (not_53_out, op[2]);
  not not_54 (not_54_out, op[6]);
  not not_55 (not_55_out, op[3]);
  not not_56 (not_56_out, op[4]);
  and and_16 (and_16_out, not_54_out, op[6], not_56_out, not_55_out, not_53_out);
  not not_57 (not_57_out, op[2]);
  or or_6 (ExtOp[1], and_16_out, and_18_out);
  not not_58 (not_58_out, op[2]);
  not not_59 (not_59_out, op[4]);
  not not_60 (not_60_out, op[3]);
  not not_61 (not_61_out, op[3]);
  not not_62 (not_62_out, op[6]);
  and and_17 (and_17_out, not_62_out, op[6], op[4], not_60_out, op[2]);
  and and_18 (and_18_out, op[6], op[6], not_59_out, not_61_out, not_58_out);
  not not_63 (not_63_out, op[3]);
  not not_64 (not_64_out, op[2]);
  not not_65 (not_65_out, op[4]);
  and and_19 (and_19_out, op[6], op[6], not_65_out, not_63_out, not_64_out);
  or or_7 (ExtOp[0], and_17_out, and_19_out);

  assign ALUBSrc[0] = ALUASrs;
  assign ExtOp[2] = ALUASrs;
  assign Jump = ALUASrs;
  assign op[5] = op[6];
endmodule
