// Logisim project Lab6.circ as structural Verilog: 5 circuits, main circuit main
module main (
  output [31:0] out_1,
  output [2:0] out_2,
  output [1:0] out_3,
  output [31:0] pc,
  output [6:0] out_5,
  output out_6,
  output [4:0] out_7,
  output [31:0] out_8,
  output [3:0] out_9,
  output [2:0] out_10,
  output out_11,
  output [4:0] out_12,
  output [31:0] Instr,
  output [31:0] out_14,
  output out_15,
  output [4:0] out_16,
  output out_17,
  output [6:0] out_18,
  output out_19,
  output [31:0] out_20,
  output out_21,
  output [31:0] Imm
);

  wire and_1_out, Clk, not_1_out, not_2_out, or_1_out, Reset, ZERO;
  wire [31:0] adder_1_out, multiplexer_1_out, multiplexer_2_out, multiplexer_3_out, ram_1_data, undriven;

  not not_1 (not_1_out, Clk);
  and and_1 (and_1_out, out_15, ZERO);
  or or_1 (or_1_out, and_1_out, out_11);
  _32_32Reg u_32_32reg_1 (
    .Reset(Reset), .R1_num(out_12), .Reg2Out(out_14), .R2_num(out_16), .Din(out_1), .Reg1Out(out_8),
    .Write_Reg_num(out_7), .Write_Enable(out_21), .Clock(Clk));
  Button button_1 (.out(Reset));
  Clock clock_1 (.out(Clk));
  Register #(.width(32), .Select("low")) u_PC (.D(adder_1_out), .Q(pc), .clk(not_1_out), .clr(Reset));  // open: en
  Multiplexer #(.width(32), .enable("false")) multiplexer_1 (
    .in0(32'h4), .in1(Imm), .out(multiplexer_1_out), .sel(or_1_out));
  Adder #(.width(32)) adder_1 (.a(pc), .b(multiplexer_1_out), .out(adder_1_out));  // open: cin, cout
  ROM #(.addrWidth(24), .dataWidth(32), .Select("low")) rom_1 (.addr(pc[25:2]), .data(Instr));
  Multiplexer #(.width(32), .enable("false")) multiplexer_2 (
    .in0(out_8), .in1(pc), .out(multiplexer_2_out), .sel(out_6));
  ALU alu_1 (.Zero(ZERO), .Result(out_20), .A(multiplexer_2_out), .B(multiplexer_3_out), .ALUctr(out_9));
  Multiplexer #(.select(2), .width(32), .enable("false")) multiplexer_3 (
    .in0(out_14), .in1(32'h4), .in2(Imm), .in3(undriven), .out(multiplexer_3_out), .sel(out_3));
  \指令解析  \u_指令解析_1  (
    .\输入指令 (Instr), .ExtOp(out_2), .op(out_5), .Rd(out_7), .funct3(out_10), .Rs1(out_12), .Rs2(out_16),
    .funct7(out_18), .Imm(Imm));
  Controller controller_1 (
    .funct3(out_10), .op(out_5), .Branch(out_15), .Jump(out_11), .ALUASrs(out_6), .ALUBSrc(out_3),
    .ALUctr(out_9), .MemtoReg(out_19), .RegWr(out_21), .MemWr(out_17), .ExtOp(out_2));
  not not_2 (not_2_out, Clk);
  RAM #(.addrWidth(24), .dataWidth(32), .bus("separate"), .Select("low")) ram_1 (
    .addr(out_20[25:2]), .din(out_14), .data(ram_1_data), .str(out_17), .clk(not_2_out), .clr(Reset));  // open: sel, ld
  Multiplexer #(.width(32), .enable("false")) multiplexer_4 (.in0(out_20), .in1(ram_1_data), .out(out_1), .sel(out_19));

  // Other names for the same wires on the sheet: ALUASrc = out_6; ALUBSrc[1:0] = out_3; ALUctr[3:0] = out_9;
  //   Branch = out_15; busA[31:0] = out_8; busB[31:0] = out_14; busW[31:0] = out_1; ExtOp[2:0] = out_2;
  //   funct3[2:0] = out_10; funct7[6:0] = out_18; Jump = out_11; MemtoReg = out_19; MemWr = out_17; op[6:0] = out_5;
  //   Rd[4:0] = out_7; RegWr = out_21; Result[31:0] = out_20; Rs1[4:0] = out_12; Rs2[4:0] = out_16

  // Notes on the sheet:
  //   contents of rom_1 (hex, n*v repeats v):
  //   2183 106293 106113 520233 328663 2282b3 ff5ff06f 402223 6f
endmodule

module \指令解析  (
  input  [31:0] \输入指令 ,
  input  [2:0] ExtOp,
  output [31:0] Imm,
  output [6:0] op,
  output [4:0] Rd,
  output [2:0] funct3,
  output [4:0] Rs1,
  output [4:0] Rs2,
  output [6:0] funct7
);

  InstrTolmm instrtolmm_1 (.Instr(\输入指令 ), .Extop(ExtOp), .imm(Imm));

  assign funct3 = \输入指令 [14:12];
  assign funct7 = \输入指令 [31:25];
  assign op = \输入指令 [6:0];
  assign Rd = \输入指令 [11:7];
  assign Rs1 = \输入指令 [19:15];
  assign Rs2 = \输入指令 [24:20];
endmodule

module Controller (
  input  [2:0] funct3,
  input  [6:0] op,
  output Branch,
  output Jump,
  output ALUASrs,
  output [1:0] ALUBSrc,
  output [3:0] ALUctr,
  output MemtoReg,
  output RegWr,
  output MemWr,
  output [2:0] ExtOp
);

  wire and_3_out, and_4_out, and_5_out, and_6_out, and_7_out, and_8_out, and_9_out, and_10_out, and_11_out,
       and_13_out, and_14_out, and_16_out, and_17_out, and_18_out, and_19_out, not_1_out, not_2_out,
       not_3_out, not_4_out, not_5_out, not_6_out, not_7_out, not_8_out, not_9_out, not_10_out, not_11_out,
       not_12_out, not_13_out, not_14_out, not_15_out, not_16_out, not_17_out, not_18_out, not_19_out,
       not_20_out, not_21_out, not_22_out, not_23_out, not_24_out, not_25_out, not_26_out, not_27_out,
       not_28_out, not_29_out, not_30_out, not_31_out, not_32_out, not_33_out, not_34_out, not_35_out,
       not_36_out, not_37_out, not_38_out, not_39_out, not_40_out, not_41_out, not_42_out, not_43_out,
       not_44_out, not_45_out, not_46_out, not_47_out, not_48_out, not_49_out, not_50_out, not_51_out,
       not_52_out, not_53_out, not_54_out, not_55_out, not_56_out, not_57_out, not_58_out, not_59_out,
       not_60_out, not_61_out, not_62_out, not_63_out, not_64_out, not_65_out;

  not not_1 (not_1_out, op[3]);
  not not_2 (not_2_out, op[4]);
  not not_3 (not_3_out, op[2]);
  and and_1 (Branch, op[6], op[5], not_2_out, not_1_out, not_3_out, op[1], op[0]);
  not not_4 (not_4_out, op[4]);
  and and_2 (ALUASrs, op[6], op[5], not_4_out, op[3], op[2], op[1], op[0]);
  not not_5 (not_5_out, op[5]);
  not not_6 (not_6_out, op[6]);
  not not_7 (not_7_out, op[3]);
  and and_3 (and_3_out, not_6_out, not_5_out, op[4], not_7_out, not_10_out);
  not not_8 (not_8_out, op[5]);
  not not_9 (not_9_out, op[3]);
  not not_10 (not_10_out, op[2]);
  not not_11 (not_11_out, op[6]);
  not not_12 (not_12_out, op[6]);
  and and_4 (and_4_out, not_12_out, op[5], op[4], not_9_out, op[2]);
  or or_1 (ALUBSrc[1], and_3_out, and_4_out, and_6_out, and_5_out);
  not not_13 (not_13_out, op[4]);
  not not_14 (not_14_out, op[4]);
  not not_15 (not_15_out, op[2]);
  not not_16 (not_16_out, op[3]);
  not not_17 (not_17_out, op[3]);
  not not_18 (not_18_out, op[2]);
  not not_19 (not_19_out, op[6]);
  and and_5 (and_5_out, not_19_out, op[5], not_14_out, not_16_out, not_18_out);
  and and_6 (and_6_out, not_11_out, not_8_out, not_13_out, not_17_out, not_15_out);
  not not_20 (not_20_out, op[3]);
  not not_21 (not_21_out, op[6]);
  and and_7 (and_7_out, not_21_out, op[5], op[4], not_20_out, op[2]);
  or or_2 (ALUctr[3], and_7_out, and_8_out);
  not not_22 (not_22_out, op[6]);
  not not_23 (not_23_out, op[2]);
  not not_24 (not_24_out, op[4]);
  not not_25 (not_25_out, op[3]);
  not not_26 (not_26_out, op[5]);
  and and_8 (and_8_out, op[6], op[5], not_24_out, not_25_out, not_23_out);
  and and_9 (and_9_out, not_22_out, not_26_out, op[4], not_30_out, not_27_out);
  or or_3 (ALUctr[2], and_7_out, and_9_out);
  not not_27 (not_27_out, op[2]);
  not not_28 (not_28_out, op[6]);
  not not_29 (not_29_out, op[3]);
  not not_30 (not_30_out, op[3]);
  and and_10 (and_10_out, not_28_out, op[5], op[4], not_29_out, not_35_out, not_34_out, funct3[1], not_31_out);
  or or_4 (ALUctr[1], and_7_out, and_9_out, and_10_out, and_11_out);
  not not_31 (not_31_out, funct3[0]);
  not not_32 (not_32_out, op[6]);
  not not_33 (not_33_out, op[3]);
  not not_34 (not_34_out, funct3[2]);
  not not_35 (not_35_out, op[2]);
  or or_5 (ALUctr[0], and_7_out, and_11_out);
  not not_36 (not_36_out, op[2]);
  not not_37 (not_37_out, funct3[2]);
  and and_11 (and_11_out, not_32_out, op[5], op[4], not_33_out, not_36_out, not_37_out, funct3[1], funct3[0]);
  not not_38 (not_38_out, op[5]);
  not not_39 (not_39_out, op[6]);
  not not_40 (not_40_out, op[4]);
  and and_12 (MemtoReg, not_39_out, not_38_out, not_40_out, not_46_out, not_45_out);
  not not_41 (not_41_out, op[2]);
  not not_42 (not_42_out, op[3]);
  not not_43 (not_43_out, op[4]);
  not not_44 (not_44_out, op[6]);
  and and_13 (and_13_out, not_44_out, op[5], not_43_out, not_42_out, not_41_out);
  not not_45 (not_45_out, op[2]);
  not not_46 (not_46_out, op[3]);
  nor nor_1 (RegWr, and_13_out, and_14_out);
  not not_47 (not_47_out, op[4]);
  not not_48 (not_48_out, op[2]);
  not not_49 (not_49_out, op[3]);
  and and_14 (and_14_out, op[6], op[5], not_47_out, not_49_out, not_48_out);
  not not_50 (not_50_out, op[4]);
  not not_51 (not_51_out, op[3]);
  not not_52 (not_52_out, op[6]);
  and and_15 (MemWr, not_52_out, op[5], not_50_out, not_51_out, not_57_out);
  not not_53 (not_53_out, op[2]);
  not not_54 (not_54_out, op[6]);
  not not_55 (not_55_out, op[4]);
  not not_56 (not_56_out, op[3]);
  and and_16 (and_16_out, not_54_out, op[5], not_55_out, not_56_out, not_53_out);
  not not_57 (not_57_out, op[2]);
  or or_6 (ExtOp[1], and_16_out, and_18_out);
  not not_58 (not_58_out, op[3]);
  not not_59 (not_59_out, op[2]);
  not not_60 (not_60_out, op[3]);
  not not_61 (not_61_out, op[4]);
  not not_62 (not_62_out, op[6]);
  and and_17 (and_17_out, not_62_out, op[5], op[4], not_58_out, op[2]);
  and and_18 (and_18_out, op[6], op[5], not_61_out, not_60_out, not_59_out);
  not not_63 (not_63_out, op[3]);
  not not_64 (not_64_out, op[2]);
  not not_65 (not_65_out, op[4]);
  and and_19 (and_19_out, op[6], op[5], not_65_out, not_63_out, not_64_out);
  or or_7 (ExtOp[0], and_17_out, and_19_out);

  assign ALUBSrc[0] = ALUASrs;
  assign ExtOp[2] = ALUASrs;
  assign Jump = ALUASrs;
endmodule

module temp (
  output [31:0] out_1,
  output [2:0] out_2,
  output [1:0] out_3,
  output [31:0] pc,
  output [6:0] out_5,
  output out_6,
  output [4:0] out_7,
  output [31:0] out_8,
  output [3:0] out_9,
  output [2:0] out_10,
  output out_11,
  output [4:0] out_12,
  output [31:0] Instr,
  output [31:0] out_14,
  output out_15,
  output [4:0] out_16,
  output out_17,
  output [6:0] out_18,
  output out_19,
  output [31:0] out_20,
  output out_21,
  output [31:0] Imm
);

  wire and_1_out, Clk, not_1_out, not_2_out, or_1_out, Reset, ZERO;
  wire [31:0] adder_1_out, multiplexer_1_out, multiplexer_2_out, multiplexer_3_out, ram_1_data, undriven;

  not not_1 (not_1_out, Clk);
  and and_1 (and_1_out, out_15, ZERO);
  or or_1 (or_1_out, and_1_out, out_11);
  _32_32Regfile u_32_32regfile_1 (
    .R1_num(out_12), .R2_num(out_16), .Write_Reg_num(out_7), .Write_Enable(out_21), .Clock(Clk), .Din(out_1),
    .Reg1Out(out_8), .Reg2Out(out_14), .Reset(Reset));
  Button button_1 (.out(Reset));
  Clock clock_1 (.out(Clk));
  Register #(.width(32), .Select("low")) u_PC (.D(adder_1_out), .Q(pc), .clk(not_1_out), .clr(Reset));  // open: en
  Multiplexer #(.width(32), .enable("false")) multiplexer_1 (
    .in0(32'h4), .in1(Imm), .out(multiplexer_1_out), .sel(or_1_out));
  Adder #(.width(32)) adder_1 (.a(pc), .b(multiplexer_1_out), .out(adder_1_out));  // open: cin, cout
  ROM #(.addrWidth(24), .dataWidth(32), .Select("low")) rom_1 (.addr(pc[25:2]), .data(Instr));
  Multiplexer #(.width(32), .enable("false")) multiplexer_2 (
    .in0(out_8), .in1(pc), .out(multiplexer_2_out), .sel(out_6));
  ALU alu_1 (.Zero(ZERO), .Result(out_20), .A(multiplexer_2_out), .B(multiplexer_3_out), .ALUctr(out_9));
  Multiplexer #(.select(2), .width(32), .enable("false")) multiplexer_3 (
    .in0(out_14), .in1(32'h4), .in2(Imm), .in3(undriven), .out(multiplexer_3_out), .sel(out_3));
  \指令解析  \u_指令解析_1  (
    .\输入指令 (Instr), .ExtOp(out_2), .op(out_5), .Rd(out_7), .funct3(out_10), .Rs1(out_12), .Rs2(out_16),
    .funct7(out_18), .Imm(Imm));
  Controller controller_1 (
    .funct3(out_10), .op(out_5), .Branch(out_15), .Jump(out_11), .ALUASrs(out_6), .ALUBSrc(out_3),
    .ALUctr(out_9), .MemtoReg(out_19), .RegWr(out_21), .MemWr(out_17), .ExtOp(out_2));
  not not_2 (not_2_out, Clk);
  RAM #(.addrWidth(24), .dataWidth(32), .bus("separate"), .Select("low")) ram_1 (
    .addr(out_20[25:2]), .din(out_14), .data(ram_1_data), .str(out_17), .clk(not_2_out), .clr(Reset));  // open: sel, ld
  Multiplexer #(.width(32), .enable("false")) multiplexer_4 (.in0(out_20), .in1(ram_1_data), .out(out_1), .sel(out_19));

  // Other names for the same wires on the sheet: ALUASrc = out_6; ALUBSrc[1:0] = out_3; ALUctr[3:0] = out_9;
  //   Branch = out_15; busA[31:0] = out_8; busB[31:0] = out_14; busW[31:0] = out_1; ExtOp[2:0] = out_2;
  //   funct3[2:0] = out_10; funct7[6:0] = out_18; Jump = out_11; MemtoReg = out_19; MemWr = out_17; op[6:0] = out_5;
  //   Rd[4:0] = out_7; RegWr = out_21; Result[31:0] = out_20; Rs1[4:0] = out_12; Rs2[4:0] = out_16

  // Notes on the sheet:
  //   contents of rom_1 (hex, n*v repeats v):
  //   2183 106293 106113 520233 328663 2282b3 ff5ff06f 402223 6f
endmodule

module _32_32Reg (
  input  Reset,
  input  [4:0] R1_num,
  input  [4:0] R2_num,
  input  [31:0] Din,
  input  [4:0] Write_Reg_num,
  input  Write_Enable,
  input  Clock,
  output [31:0] Reg2Out,
  output [31:0] Reg1Out
);

  wire and_1_out, and_2_out, and_3_out, and_4_out, and_5_out, and_6_out, and_7_out, and_8_out, and_9_out,
       and_10_out, and_11_out, and_12_out, and_13_out, and_14_out, and_15_out, and_16_out, and_17_out,
       and_18_out, and_19_out, and_20_out, and_21_out, and_22_out, and_23_out, and_24_out, and_25_out,
       and_26_out, and_27_out, and_28_out, and_29_out, and_30_out, and_31_out, and_32_out, decoder_1_out0,
       decoder_1_out1, decoder_1_out2, decoder_1_out3, decoder_1_out4, decoder_1_out5, decoder_1_out6,
       decoder_1_out7, decoder_1_out8, decoder_1_out9, decoder_1_out10, decoder_1_out11, decoder_1_out12,
       decoder_1_out13, decoder_1_out14, decoder_1_out15, decoder_1_out16, decoder_1_out17, decoder_1_out18,
       decoder_1_out19, decoder_1_out20, decoder_1_out21, decoder_1_out22, decoder_1_out23, decoder_1_out24,
       decoder_1_out25, decoder_1_out26, decoder_1_out27, decoder_1_out28, decoder_1_out29, decoder_1_out30,
       decoder_1_out31, undriven;
  wire [31:0] register_1_q, register_2_q, register_3_q, register_4_q, register_5_q, register_6_q,
       register_7_q, register_8_q, register_9_q, register_10_q, register_11_q, register_12_q, register_13_q,
       register_14_q, register_15_q, register_16_q, register_17_q, register_18_q, register_19_q,
       register_20_q, register_21_q, register_22_q, register_23_q, register_24_q, register_25_q,
       register_26_q, register_27_q, register_28_q, register_29_q, register_30_q, register_31_q,
       register_32_q;

  Decoder #(.select(5), .enable("false")) decoder_1 (
    .out0(decoder_1_out0), .out1(decoder_1_out1), .out2(decoder_1_out2), .out3(decoder_1_out3),
    .out4(decoder_1_out4), .out5(decoder_1_out5), .out6(decoder_1_out6), .out7(decoder_1_out7),
    .out8(decoder_1_out8), .out9(decoder_1_out9), .out10(decoder_1_out10), .out11(decoder_1_out11),
    .out12(decoder_1_out12), .out13(decoder_1_out13), .out14(decoder_1_out14), .out15(decoder_1_out15),
    .out16(decoder_1_out16), .out17(decoder_1_out17), .out18(decoder_1_out18), .out19(decoder_1_out19),
    .out20(decoder_1_out20), .out21(decoder_1_out21), .out22(decoder_1_out22), .out23(decoder_1_out23),
    .out24(decoder_1_out24), .out25(decoder_1_out25), .out26(decoder_1_out26), .out27(decoder_1_out27),
    .out28(decoder_1_out28), .out29(decoder_1_out29), .out30(decoder_1_out30), .out31(decoder_1_out31),
    .sel(Write_Reg_num));
  Register #(.width(32), .Select("low")) register_1 (.D(Din), .Q(register_1_q), .clr(1'b1));  // open: en, clk
  and and_1 (and_1_out, Write_Enable, Clock, decoder_1_out0);
  Register #(.width(32), .Select("low")) register_2 (
    .D(Din), .Q(register_2_q), .clk(and_2_out), .clr(Reset), .preset(Reset));  // open: en, cs
  and and_2 (and_2_out, Write_Enable, Clock, decoder_1_out1);
  Register #(.width(32), .Select("low")) register_3 (
    .D(Din), .Q(register_3_q), .clk(and_3_out), .clr(Reset), .preset(Reset));  // open: en, cs
  and and_3 (and_3_out, Write_Enable, Clock, decoder_1_out2);
  Register #(.width(32), .Select("low")) register_4 (
    .D(Din), .Q(register_4_q), .clk(and_4_out), .clr(Reset), .preset(undriven));  // open: en, cs
  and and_4 (and_4_out, Write_Enable, Clock, decoder_1_out3);
  Register #(.width(32), .Select("low")) register_5 (
    .D(Din), .Q(register_5_q), .clk(and_5_out), .clr(Reset));  // open: en
  and and_5 (and_5_out, Write_Enable, Clock, decoder_1_out4);
  Register #(.width(32), .Select("low")) register_6 (
    .D(Din), .Q(register_6_q), .clk(and_6_out), .clr(Reset));  // open: en
  and and_6 (and_6_out, Write_Enable, Clock, decoder_1_out5);
  Register #(.width(32), .Select("low")) register_7 (
    .D(Din), .Q(register_7_q), .clk(and_7_out), .clr(Reset));  // open: en
  and and_7 (and_7_out, Write_Enable, Clock, decoder_1_out6);
  Register #(.width(32), .Select("low")) register_8 (
    .D(Din), .Q(register_8_q), .clk(and_8_out), .clr(Reset));  // open: en
  and and_8 (and_8_out, Write_Enable, Clock, decoder_1_out7);
  Register #(.width(32), .Select("low")) register_9 (
    .D(Din), .Q(register_9_q), .clk(and_9_out), .clr(Reset));  // open: en
  and and_9 (and_9_out, Write_Enable, Clock, decoder_1_out8);
  Register #(.width(32), .Select("low")) register_10 (
    .D(Din), .Q(register_10_q), .clk(and_10_out), .clr(Reset));  // open: en
  and and_10 (and_10_out, Write_Enable, Clock, decoder_1_out9);
  Register #(.width(32), .Select("low")) register_11 (
    .D(Din), .Q(register_11_q), .clk(and_11_out), .clr(Reset));  // open: en
  and and_11 (and_11_out, Write_Enable, Clock, decoder_1_out10);
  Register #(.width(32), .Select("low")) register_12 (
    .D(Din), .Q(register_12_q), .clk(and_12_out), .clr(Reset));  // open: en
  and and_12 (and_12_out, Write_Enable, Clock, decoder_1_out11);
  Register #(.width(32), .Select("low")) register_13 (
    .D(Din), .Q(register_13_q), .clk(and_13_out), .clr(Reset));  // open: en
  and and_13 (and_13_out, Write_Enable, Clock, decoder_1_out12);
  Register #(.width(32), .Select("low")) register_14 (
    .D(Din), .Q(register_14_q), .clk(and_14_out), .clr(Reset));  // open: en
  and and_14 (and_14_out, Write_Enable, Clock, decoder_1_out13);
  Register #(.width(32), .Select("low")) register_15 (
    .D(Din), .Q(register_15_q), .clk(and_15_out), .clr(Reset));  // open: en
  and and_15 (and_15_out, Write_Enable, Clock, decoder_1_out14);
  Register #(.width(32), .Select("low")) register_16 (
    .D(Din), .Q(register_16_q), .clk(and_16_out), .clr(Reset));  // open: en
  and and_16 (and_16_out, Write_Enable, Clock, decoder_1_out15);
  Register #(.width(32), .Select("low")) register_17 (
    .D(Din), .Q(register_17_q), .clk(and_17_out), .clr(Reset));  // open: en
  and and_17 (and_17_out, Write_Enable, Clock, decoder_1_out16);
  Register #(.width(32), .Select("low")) register_18 (
    .D(Din), .Q(register_18_q), .clk(and_18_out), .clr(Reset));  // open: en
  and and_18 (and_18_out, Write_Enable, Clock, decoder_1_out17);
  Register #(.width(32), .Select("low")) register_19 (
    .D(Din), .Q(register_19_q), .clk(and_19_out), .clr(Reset));  // open: en
  and and_19 (and_19_out, Write_Enable, Clock, decoder_1_out18);
  Register #(.width(32), .Select("low")) register_20 (
    .D(Din), .Q(register_20_q), .clk(and_20_out), .clr(Reset));  // open: en
  and and_20 (and_20_out, Write_Enable, Clock, decoder_1_out19);
  Register #(.width(32), .Select("low")) register_21 (
    .D(Din), .Q(register_21_q), .clk(and_21_out), .clr(Reset));  // open: en
  and and_21 (and_21_out, Write_Enable, Clock, decoder_1_out20);
  Register #(.width(32), .Select("low")) register_22 (
    .D(Din), .Q(register_22_q), .clk(and_22_out), .clr(Reset));  // open: en
  and and_22 (and_22_out, Write_Enable, Clock, decoder_1_out21);
  Register #(.width(32), .Select("low")) register_23 (
    .D(Din), .Q(register_23_q), .clk(and_23_out), .clr(Reset));  // open: en
  and and_23 (and_23_out, Write_Enable, Clock, decoder_1_out22);
  Register #(.width(32), .Select("low")) register_24 (
    .D(Din), .Q(register_24_q), .clk(and_24_out), .clr(Reset));  // open: en
  and and_24 (and_24_out, Write_Enable, Clock, decoder_1_out23);
  Register #(.width(32), .Select("low")) register_25 (
    .D(Din), .Q(register_25_q), .clk(and_25_out), .clr(Reset));  // open: en
  and and_25 (and_25_out, Write_Enable, Clock, decoder_1_out24);
  Register #(.width(32), .Select("low")) register_26 (
    .D(Din), .Q(register_26_q), .clk(and_26_out), .clr(Reset));  // open: en
  and and_26 (and_26_out, Write_Enable, Clock, decoder_1_out25);
  Register #(.width(32), .Select("low")) register_27 (
    .D(Din), .Q(register_27_q), .clk(and_27_out), .clr(Reset));  // open: en
  and and_27 (and_27_out, Write_Enable, Clock, decoder_1_out26);
  Register #(.width(32), .Select("low")) register_28 (
    .D(Din), .Q(register_28_q), .clk(and_28_out), .clr(Reset));  // open: en
  and and_28 (and_28_out, Write_Enable, Clock, decoder_1_out27);
  Register #(.width(32), .Select("low")) register_29 (
    .D(Din), .Q(register_29_q), .clk(and_29_out), .clr(Reset));  // open: en
  and and_29 (and_29_out, Write_Enable, Clock, decoder_1_out28);
  Register #(.width(32), .Select("low")) register_30 (
    .D(Din), .Q(register_30_q), .clk(and_30_out), .clr(Reset));  // open: en
  and and_30 (and_30_out, Write_Enable, Clock, decoder_1_out29);
  Register #(.width(32), .Select("low")) register_31 (
    .D(Din), .Q(register_31_q), .clk(and_31_out), .clr(Reset));  // open: en
  and and_31 (and_31_out, Write_Enable, Clock, decoder_1_out30);
  Register #(.width(32), .Select("low")) register_32 (
    .D(Din), .Q(register_32_q), .clk(and_32_out), .clr(Reset));  // open: en
  and and_32 (and_32_out, Write_Enable, Clock, decoder_1_out31);
  Multiplexer #(.select(5), .width(32), .enable("false")) multiplexer_1 (
    .in0(register_1_q), .in1(register_2_q), .in2(register_3_q), .in3(register_4_q), .in4(register_5_q),
    .in5(register_6_q), .in6(register_7_q), .in7(register_8_q), .in8(register_9_q), .in9(register_10_q),
    .in10(register_11_q), .in11(register_12_q), .in12(register_13_q), .in13(register_14_q),
    .in14(register_15_q), .in15(register_16_q), .in16(register_17_q), .in17(register_18_q),
    .in18(register_19_q), .in19(register_20_q), .in20(register_21_q), .in21(register_22_q),
    .in22(register_23_q), .in23(register_24_q), .in24(register_25_q), .in25(register_26_q),
    .in26(register_27_q), .in27(register_28_q), .in28(register_29_q), .in29(register_30_q),
    .in30(register_31_q), .in31(register_32_q), .out(Reg1Out), .sel(R1_num));
  Multiplexer #(.select(5), .width(32), .enable("false")) multiplexer_2 (
    .in0(register_1_q), .in1(register_2_q), .in2(register_3_q), .in3(register_4_q), .in4(register_5_q),
    .in5(register_6_q), .in6(register_7_q), .in7(register_8_q), .in8(register_9_q), .in9(register_10_q),
    .in10(register_11_q), .in11(register_12_q), .in12(register_13_q), .in13(register_14_q),
    .in14(register_15_q), .in15(register_16_q), .in16(register_17_q), .in17(register_18_q),
    .in18(register_19_q), .in19(register_20_q), .in20(register_21_q), .in21(register_22_q),
    .in22(register_23_q), .in23(register_24_q), .in24(register_25_q), .in25(register_26_q),
    .in26(register_27_q), .in27(register_28_q), .in28(register_29_q), .in29(register_30_q),
    .in30(register_31_q), .in31(register_32_q), .out(Reg2Out), .sel(R2_num));

  // Other names for the same wires on the sheet: CLK = Clock; RA[4:0] = R1_num; RB[4:0] = R2_num; RDA[31:0] = Reg1Out;
  //   RDB[31:0] = Reg2Out; RW[4:0] = Write_Reg_num; WE = Write_Enable
endmodule
