// Logisim project reg-file.circ as structural Verilog: 2 circuits, main circuit main
module main (
  input  [4:0] in_1,
  input  [4:0] in_2,
  input  [31:0] in_3,
  output [31:0] out_4
);

  wire clock_1_out;

  Clock clock_1 (.out(clock_1_out));
  _32_32Regfile u_32_32regfile_1 (
    .R1_num(in_1), .Write_Reg_num(in_2), .Write_Enable(1'b1), .Clock(clock_1_out), .Din(in_3), .Reg1Out(out_4));  // open: R2_num, Reg2Out, Reset
endmodule

module _32_32Regfile (
  input  Reset,
  input  [4:0] R1_num,
  input  [4:0] R2_num,
  input  [31:0] Din,
  input  [4:0] Write_Reg_num,
  input  Write_Enable,
  input  Clock,
  output [31:0] Reg2Out,
  output [31:0] Reg1Out
);

  wire and_1_out, and_2_out, and_3_out, and_4_out, and_5_out, and_6_out, and_7_out, and_8_out, and_9_out,
       and_10_out, and_11_out, and_12_out, and_13_out, and_14_out, and_15_out, and_16_out, and_17_out,
       and_18_out, and_19_out, and_20_out, and_21_out, and_22_out, and_23_out, and_24_out, and_25_out,
       and_26_out, and_27_out, and_28_out, and_29_out, and_30_out, and_31_out, and_32_out, decoder_1_out0,
       decoder_1_out1, decoder_1_out2, decoder_1_out3, decoder_1_out4, decoder_1_out5, decoder_1_out6,
       decoder_1_out7, decoder_1_out8, decoder_1_out9, decoder_1_out10, decoder_1_out11, decoder_1_out12,
       decoder_1_out13, decoder_1_out14, decoder_1_out15, decoder_1_out16, decoder_1_out17, decoder_1_out18,
       decoder_1_out19, decoder_1_out20, decoder_1_out21, decoder_1_out22, decoder_1_out23, decoder_1_out24,
       decoder_1_out25, decoder_1_out26, decoder_1_out27, decoder_1_out28, decoder_1_out29, decoder_1_out30,
       decoder_1_out31, undriven;
  wire [31:0] register_1_q, register_2_q, register_3_q, register_4_q, register_5_q, register_6_q,
       register_7_q, register_8_q, register_9_q, register_10_q, register_11_q, register_12_q, register_13_q,
       register_14_q, register_15_q, register_16_q, register_17_q, register_18_q, register_19_q,
       register_20_q, register_21_q, register_22_q, register_23_q, register_24_q, register_25_q,
       register_26_q, register_27_q, register_28_q, register_29_q, register_30_q, register_31_q,
       register_32_q;

  Decoder #(.select(5), .enable("false")) decoder_1 (
    .out0(decoder_1_out0), .out1(decoder_1_out1), .out2(decoder_1_out2), .out3(decoder_1_out3),
    .out4(decoder_1_out4), .out5(decoder_1_out5), .out6(decoder_1_out6), .out7(decoder_1_out7),
    .out8(decoder_1_out8), .out9(decoder_1_out9), .out10(decoder_1_out10), .out11(decoder_1_out11),
    .out12(decoder_1_out12), .out13(decoder_1_out13), .out14(decoder_1_out14), .out15(decoder_1_out15),
    .out16(decoder_1_out16), .out17(decoder_1_out17), .out18(decoder_1_out18), .out19(decoder_1_out19),
    .out20(decoder_1_out20), .out21(decoder_1_out21), .out22(decoder_1_out22), .out23(decoder_1_out23),
    .out24(decoder_1_out24), .out25(decoder_1_out25), .out26(decoder_1_out26), .out27(decoder_1_out27),
    .out28(decoder_1_out28), .out29(decoder_1_out29), .out30(decoder_1_out30), .out31(decoder_1_out31),
    .sel(Write_Reg_num));
  Register #(.width(32), .Select("low")) register_1 (.D(Din), .Q(register_1_q), .clr(1'b1));  // open: en, clk
  and and_1 (and_1_out, Write_Enable, Clock, decoder_1_out0);
  Register #(.width(32), .Select("low")) register_2 (
    .D(Din), .Q(register_2_q), .clk(and_2_out), .clr(Reset), .preset(Reset));  // open: en, cs
  and and_2 (and_2_out, Write_Enable, Clock, decoder_1_out1);
  Register #(.width(32), .Select("low")) register_3 (
    .D(Din), .Q(register_3_q), .clk(and_3_out), .clr(Reset), .preset(Reset));  // open: en, cs
  and and_3 (and_3_out, Write_Enable, Clock, decoder_1_out2);
  Register #(.width(32), .Select("low")) register_4 (
    .D(Din), .Q(register_4_q), .clk(and_4_out), .clr(Reset), .preset(undriven));  // open: en, cs
  and and_4 (and_4_out, Write_Enable, Clock, decoder_1_out3);
  Register #(.width(32), .Select("low")) register_5 (
    .D(Din), .Q(register_5_q), .clk(and_5_out), .clr(Reset));  // open: en
  and and_5 (and_5_out, Write_Enable, Clock, decoder_1_out4);
  Register #(.width(32), .Select("low")) register_6 (
    .D(Din), .Q(register_6_q), .clk(and_6_out), .clr(Reset));  // open: en
  and and_6 (and_6_out, Write_Enable, Clock, decoder_1_out5);
  Register #(.width(32), .Select("low")) register_7 (
    .D(Din), .Q(register_7_q), .clk(and_7_out), .clr(Reset));  // open: en
  and and_7 (and_7_out, Write_Enable, Clock, decoder_1_out6);
  Register #(.width(32), .Select("low")) register_8 (
    .D(Din), .Q(register_8_q), .clk(and_8_out), .clr(Reset));  // open: en
  and and_8 (and_8_out, Write_Enable, Clock, decoder_1_out7);
  Register #(.width(32), .Select("low")) register_9 (
    .D(Din), .Q(register_9_q), .clk(and_9_out), .clr(Reset));  // open: en
  and and_9 (and_9_out, Write_Enable, Clock, decoder_1_out8);
  Register #(.width(32), .Select("low")) register_10 (
    .D(Din), .Q(register_10_q), .clk(and_10_out), .clr(Reset));  // open: en
  and and_10 (and_10_out, Write_Enable, Clock, decoder_1_out9);
  Register #(.width(32), .Select("low")) register_11 (
    .D(Din), .Q(register_11_q), .clk(and_11_out), .clr(Reset));  // open: en
  and and_11 (and_11_out, Write_Enable, Clock, decoder_1_out10);
  Register #(.width(32), .Select("low")) register_12 (
    .D(Din), .Q(register_12_q), .clk(and_12_out), .clr(Reset));  // open: en
  and and_12 (and_12_out, Write_Enable, Clock, decoder_1_out11);
  Register #(.width(32), .Select("low")) register_13 (
    .D(Din), .Q(register_13_q), .clk(and_13_out), .clr(Reset));  // open: en
  and and_13 (and_13_out, Write_Enable, Clock, decoder_1_out12);
  Register #(.width(32), .Select("low")) register_14 (
    .D(Din), .Q(register_14_q), .clk(and_14_out), .clr(Reset));  // open: en
  and and_14 (and_14_out, Write_Enable, Clock, decoder_1_out13);
  Register #(.width(32), .Select("low")) register_15 (
    .D(Din), .Q(register_15_q), .clk(and_15_out), .clr(Reset));  // open: en
  and and_15 (and_15_out, Write_Enable, Clock, decoder_1_out14);
  Register #(.width(32), .Select("low")) register_16 (
    .D(Din), .Q(register_16_q), .clk(and_16_out), .clr(Reset));  // open: en
  and and_16 (and_16_out, Write_Enable, Clock, decoder_1_out15);
  Register #(.width(32), .Select("low")) register_17 (
    .D(Din), .Q(register_17_q), .clk(and_17_out), .clr(Reset));  // open: en
  and and_17 (and_17_out, Write_Enable, Clock, decoder_1_out16);
  Register #(.width(32), .Select("low")) register_18 (
    .D(Din), .Q(register_18_q), .clk(and_18_out), .clr(Reset));  // open: en
  and and_18 (and_18_out, Write_Enable, Clock, decoder_1_out17);
  Register #(.width(32), .Select("low")) register_19 (
    .D(Din), .Q(register_19_q), .clk(and_19_out), .clr(Reset));  // open: en
  and and_19 (and_19_out, Write_Enable, Clock, decoder_1_out18);
  Register #(.width(32), .Select("low")) register_20 (
    .D(Din), .Q(register_20_q), .clk(and_20_out), .clr(Reset));  // open: en
  and and_20 (and_20_out, Write_Enable, Clock, decoder_1_out19);
  Register #(.width(32), .Select("low")) register_21 (
    .D(Din), .Q(register_21_q), .clk(and_21_out), .clr(Reset));  // open: en
  and and_21 (and_21_out, Write_Enable, Clock, decoder_1_out20);
  Register #(.width(32), .Select("low")) register_22 (
    .D(Din), .Q(register_22_q), .clk(and_22_out), .clr(Reset));  // open: en
  and and_22 (and_22_out, Write_Enable, Clock, decoder_1_out21);
  Register #(.width(32), .Select("low")) register_23 (
    .D(Din), .Q(register_23_q), .clk(and_23_out), .clr(Reset));  // open: en
  and and_23 (and_23_out, Write_Enable, Clock, decoder_1_out22);
  Register #(.width(32), .Select("low")) register_24 (
    .D(Din), .Q(register_24_q), .clk(and_24_out), .clr(Reset));  // open: en
  and and_24 (and_24_out, Write_Enable, Clock, decoder_1_out23);
  Register #(.width(32), .Select("low")) register_25 (
    .D(Din), .Q(register_25_q), .clk(and_25_out), .clr(Reset));  // open: en
  and and_25 (and_25_out, Write_Enable, Clock, decoder_1_out24);
  Register #(.width(32), .Select("low")) register_26 (
    .D(Din), .Q(register_26_q), .clk(and_26_out), .clr(Reset));  // open: en
  and and_26 (and_26_out, Write_Enable, Clock, decoder_1_out25);
  Register #(.width(32), .Select("low")) register_27 (
    .D(Din), .Q(register_27_q), .clk(and_27_out), .clr(Reset));  // open: en
  and and_27 (and_27_out, Write_Enable, Clock, decoder_1_out26);
  Register #(.width(32), .Select("low")) register_28 (
    .D(Din), .Q(register_28_q), .clk(and_28_out), .clr(Reset));  // open: en
  and and_28 (and_28_out, Write_Enable, Clock, decoder_1_out27);
  Register #(.width(32), .Select("low")) register_29 (
    .D(Din), .Q(register_29_q), .clk(and_29_out), .clr(Reset));  // open: en
  and and_29 (and_29_out, Write_Enable, Clock, decoder_1_out28);
  Register #(.width(32), .Select("low")) register_30 (
    .D(Din), .Q(register_30_q), .clk(and_30_out), .clr(Reset));  // open: en
  and and_30 (and_30_out, Write_Enable, Clock, decoder_1_out29);
  Register #(.width(32), .Select("low")) register_31 (
    .D(Din), .Q(register_31_q), .clk(and_31_out), .clr(Reset));  // open: en
  and and_31 (and_31_out, Write_Enable, Clock, decoder_1_out30);
  Register #(.width(32), .Select("low")) register_32 (
    .D(Din), .Q(register_32_q), .clk(and_32_out), .clr(Reset));  // open: en
  and and_32 (and_32_out, Write_Enable, Clock, decoder_1_out31);
  Multiplexer #(.select(5), .width(32), .enable("false")) multiplexer_1 (
    .in0(register_1_q), .in1(register_2_q), .in2(register_3_q), .in3(register_4_q), .in4(register_5_q),
    .in5(register_6_q), .in6(register_7_q), .in7(register_8_q), .in8(register_9_q), .in9(register_10_q),
    .in10(register_11_q), .in11(register_12_q), .in12(register_13_q), .in13(register_14_q),
    .in14(register_15_q), .in15(register_16_q), .in16(register_17_q), .in17(register_18_q),
    .in18(register_19_q), .in19(register_20_q), .in20(register_21_q), .in21(register_22_q),
    .in22(register_23_q), .in23(register_24_q), .in24(register_25_q), .in25(register_26_q),
    .in26(register_27_q), .in27(register_28_q), .in28(register_29_q), .in29(register_30_q),
    .in30(register_31_q), .in31(register_32_q), .out(Reg1Out), .sel(R1_num));
  Multiplexer #(.select(5), .width(32), .enable("false")) multiplexer_2 (
    .in0(register_1_q), .in1(register_2_q), .in2(register_3_q), .in3(register_4_q), .in4(register_5_q),
    .in5(register_6_q), .in6(register_7_q), .in7(register_8_q), .in8(register_9_q), .in9(register_10_q),
    .in10(register_11_q), .in11(register_12_q), .in12(register_13_q), .in13(register_14_q),
    .in14(register_15_q), .in15(register_16_q), .in16(register_17_q), .in17(register_18_q),
    .in18(register_19_q), .in19(register_20_q), .in20(register_21_q), .in21(register_22_q),
    .in22(register_23_q), .in23(register_24_q), .in24(register_25_q), .in25(register_26_q),
    .in26(register_27_q), .in27(register_28_q), .in28(register_29_q), .in29(register_30_q),
    .in30(register_31_q), .in31(register_32_q), .out(Reg2Out), .sel(R2_num));

  // Other names for the same wires on the sheet: CLK = Clock; RA[4:0] = R1_num; RB[4:0] = R2_num; RDA[31:0] = Reg1Out;
  //   RDB[31:0] = Reg2Out; RW[4:0] = Write_Reg_num; WE = Write_Enable
endmodule
